// Logisim project S1-T22.circ as structural Verilog: 12 circuits, main circuit main
// LED2
module main (
  input  [1:0] ROAD_QUALITY,
  input  DRIVER_S_QUALITY,
  input  [1:0] TYPE_OF_VEHIVLE,
  input  [3:0] FUEL,
  input  [3:0] distance_travelled,
  input  in_6,
  input  [3:0] in_7,
  input  [3:0] in_8,
  input  [3:0] in_9,
  input  [3:0] in_10,
  input  DnN
);

  wire _8_bit_binary_to_BCD_h0, _8_bit_binary_to_BCD_h1, _8_bit_binary_to_BCD_h2, _8_bit_binary_to_BCD_h3,
       _8_bit_binary_to_BCD_t0, _8_bit_binary_to_BCD_t1, _8_bit_binary_to_BCD_t2, _8_bit_binary_to_BCD_t3,
       _8_bit_binary_to_BCD_u0, _8_bit_binary_to_BCD_u1, _8_bit_binary_to_BCD_u2, _8_bit_binary_to_BCD_u3,
       adder_cum_sub_out_11, adder_cum_sub_out_12, adder_cum_sub_out_13, adder_cum_sub_out_14, and_1_out,
       BCD_to_7_segment_DECODER_2_out_5, BCD_to_7_segment_DECODER_2_out_6, BCD_to_7_segment_DECODER_2_out_7,
       BCD_to_7_segment_DECODER_2_out_8, BCD_to_7_segment_DECODER_2_out_9, BCD_to_7_segment_DECODER_2_out_10,
       BCD_to_7_segment_DECODER_2_out_11, BCD_to_7_segment_DECODER_3_out_5, BCD_to_7_segment_DECODER_3_out_6,
       BCD_to_7_segment_DECODER_3_out_7, BCD_to_7_segment_DECODER_3_out_8, BCD_to_7_segment_DECODER_3_out_9,
       BCD_to_7_segment_DECODER_3_out_10, BCD_to_7_segment_DECODER_3_out_11, BCD_to_7_segment_DECODER_out_5,
       BCD_to_7_segment_DECODER_out_6, BCD_to_7_segment_DECODER_out_7, BCD_to_7_segment_DECODER_out_8,
       BCD_to_7_segment_DECODER_out_9, BCD_to_7_segment_DECODER_out_10, BCD_to_7_segment_DECODER_out_11,
       clock_1_out, clock_2_out, clock_3_out, clock_4_out, COMPARATOR_2_equal, COMPARATOR_2_less_than,
       COMPARATOR_equal, COMPARATOR_less_than, FULL_ADDER_s0, FULL_ADDER_s1, FULL_ADDER_s2, FULL_ADDER_s3,
       not_1_out, or_1_out, or_2_out;
  wire [3:0] D_flip_flop_2_lsb_2, D_flip_flop_3_lsb_2, D_flip_flop_4_lsb_2, D_flip_flop_lsb_2, divider_1_out,
       INITIAL_MODULE_out_4, INITIAL_MODULE_out_5, INITIAL_MODULE_out_6, multiplexer_1_out, multiplexer_2_out;
  wire [5:0] mileage_1_out_14;
  wire [7:0] MULTIPLIER_MODULE_2_out_9, MULTIPLIER_MODULE_out_9;

  initial_calc INITIAL_MODULE (
    .DRIVER_S_QUALITY(DRIVER_S_QUALITY), .out_4(INITIAL_MODULE_out_4), .out_5(INITIAL_MODULE_out_5),
    .out_6(INITIAL_MODULE_out_6), .ROAD_QUALITY(ROAD_QUALITY), .TYPE_OF_VEHICLE(TYPE_OF_VEHIVLE));
  Clock clock_1 (.out(clock_1_out));
  _4_bit_D_flip_flop D_flip_flop (
    .CLK(clock_1_out), .LSB(in_10[0]), .in_3(in_10[1]), .in_4(in_10[2]), .MSB(in_10[3]),
    .LSB_2(D_flip_flop_lsb_2[0]), .out_7(D_flip_flop_lsb_2[1]), .out_8(D_flip_flop_lsb_2[2]),
    .MSB_2(D_flip_flop_lsb_2[3]));
  Multiplexer #(.width(4)) multiplexer_1 (
    .in0(in_9), .in1(D_flip_flop_lsb_2), .out(multiplexer_1_out), .sel(DnN));  // open: en
  mileage mileage_1 (
    .in_1(INITIAL_MODULE_out_5[0]), .in_2(INITIAL_MODULE_out_4[0]), .in_3(INITIAL_MODULE_out_5[1]),
    .in_4(INITIAL_MODULE_out_4[1]), .in_5(INITIAL_MODULE_out_5[2]), .in_6(INITIAL_MODULE_out_4[2]),
    .in_7(INITIAL_MODULE_out_5[3]), .in_8(INITIAL_MODULE_out_4[3]), .in_9(INITIAL_MODULE_out_6[0]),
    .in_10(INITIAL_MODULE_out_6[1]), .in_11(INITIAL_MODULE_out_6[2]), .in_12(INITIAL_MODULE_out_6[3]),
    .in_13(1'b0), .out_14(mileage_1_out_14));
  Multiplexer #(.width(4)) multiplexer_2 (
    .in0(FUEL), .in1(D_flip_flop_2_lsb_2), .out(multiplexer_2_out), .sel(in_6));  // open: en
  Divider #(.width(4)) divider_1 (
    .a(distance_travelled), .b(mileage_1_out_14[3:0]), .out(divider_1_out));  // open: upper, rem
  _4_bit_multiplier MULTIPLIER_MODULE (
    .in_1(distance_travelled[0]), .in_2(distance_travelled[1]), .in_3(distance_travelled[2]),
    .in_4(distance_travelled[3]), .in_5(multiplexer_1_out[0]), .in_6(multiplexer_1_out[1]),
    .in_7(multiplexer_1_out[2]), .in_8(multiplexer_1_out[3]), .out_9(MULTIPLIER_MODULE_out_9));
  _4_bit_multiplier MULTIPLIER_MODULE_2 (
    .in_1(mileage_1_out_14[0]), .in_2(mileage_1_out_14[1]), .in_3(mileage_1_out_14[2]),
    .in_4(mileage_1_out_14[3]), .in_5(multiplexer_2_out[0]), .in_6(multiplexer_2_out[1]),
    .in_7(multiplexer_2_out[2]), .in_8(multiplexer_2_out[3]), .out_9(MULTIPLIER_MODULE_2_out_9));
  _8_bit_binary_to_BCD _8_bit_binary_to_BCD (
    .A(MULTIPLIER_MODULE_2_out_9[7]), .B(MULTIPLIER_MODULE_2_out_9[6]), .C(MULTIPLIER_MODULE_2_out_9[5]),
    .D(MULTIPLIER_MODULE_2_out_9[4]), .E(MULTIPLIER_MODULE_2_out_9[3]), .F(MULTIPLIER_MODULE_2_out_9[2]),
    .G(MULTIPLIER_MODULE_2_out_9[1]), .H(MULTIPLIER_MODULE_2_out_9[0]), .H3(_8_bit_binary_to_BCD_h3),
    .H2(_8_bit_binary_to_BCD_h2), .H1(_8_bit_binary_to_BCD_h1), .H0(_8_bit_binary_to_BCD_h0),
    .T3(_8_bit_binary_to_BCD_t3), .T2(_8_bit_binary_to_BCD_t2), .T1(_8_bit_binary_to_BCD_t1),
    .T0(_8_bit_binary_to_BCD_t0), .U3(_8_bit_binary_to_BCD_u3), .U2(_8_bit_binary_to_BCD_u2),
    .U1(_8_bit_binary_to_BCD_u1), .U0(_8_bit_binary_to_BCD_u0));
  _4_bit_D_flip_flop D_flip_flop_2 (
    .CLK(clock_2_out), .LSB(adder_cum_sub_out_14), .in_3(adder_cum_sub_out_13), .in_4(adder_cum_sub_out_12),
    .MSB(adder_cum_sub_out_11), .LSB_2(D_flip_flop_2_lsb_2[0]), .out_7(D_flip_flop_2_lsb_2[1]),
    .out_8(D_flip_flop_2_lsb_2[2]), .MSB_2(D_flip_flop_2_lsb_2[3]));
  Clock clock_2 (.out(clock_2_out));
  _4_bit_adder_cun_subtractor adder_cum_sub (
    .B3(FULL_ADDER_s0), .A3(multiplexer_2_out[3]), .B2(FULL_ADDER_s1), .A2(multiplexer_2_out[2]),
    .B1(FULL_ADDER_s2), .A1(multiplexer_2_out[1]), .B0(FULL_ADDER_s3), .A0(multiplexer_2_out[0]),
    .out_11(adder_cum_sub_out_11), .out_12(adder_cum_sub_out_12), .out_13(adder_cum_sub_out_13),
    .out_14(adder_cum_sub_out_14), .in_9(1'b1));  // open: out_10
  _4_bit_full_adder FULL_ADDER (
    .A3(divider_1_out[0]), .B3(MULTIPLIER_MODULE_out_9[0]), .A2(divider_1_out[1]),
    .B2(MULTIPLIER_MODULE_out_9[1]), .A1(divider_1_out[2]), .B1(MULTIPLIER_MODULE_out_9[2]),
    .A0(divider_1_out[3]), .B0(MULTIPLIER_MODULE_out_9[3]), .S3(FULL_ADDER_s3), .S2(FULL_ADDER_s2),
    .S1(FULL_ADDER_s1), .S0(FULL_ADDER_s0));  // open: CIN, COUT
  BCD_to_7_segment_display BCD_to_7_segment_DECODER (
    .MSB(_8_bit_binary_to_BCD_h3), .in_2(_8_bit_binary_to_BCD_h2), .in_3(_8_bit_binary_to_BCD_h1),
    .LSB(_8_bit_binary_to_BCD_h0), .out_5(BCD_to_7_segment_DECODER_out_5),
    .out_6(BCD_to_7_segment_DECODER_out_6), .out_7(BCD_to_7_segment_DECODER_out_7),
    .out_8(BCD_to_7_segment_DECODER_out_8), .out_9(BCD_to_7_segment_DECODER_out_9),
    .out_10(BCD_to_7_segment_DECODER_out_10), .out_11(BCD_to_7_segment_DECODER_out_11));
  _7_Segment_Display u_7_segment_display_1 (
    .g(BCD_to_7_segment_DECODER_out_11), .f(BCD_to_7_segment_DECODER_out_10),
    .a(BCD_to_7_segment_DECODER_out_5), .b(BCD_to_7_segment_DECODER_out_6),
    .e(BCD_to_7_segment_DECODER_out_9), .d(BCD_to_7_segment_DECODER_out_8), .c(BCD_to_7_segment_DECODER_out_7));  // open: dp
  BCD_to_7_segment_display BCD_to_7_segment_DECODER_2 (
    .MSB(_8_bit_binary_to_BCD_t3), .in_2(_8_bit_binary_to_BCD_t2), .in_3(_8_bit_binary_to_BCD_t1),
    .LSB(_8_bit_binary_to_BCD_t0), .out_5(BCD_to_7_segment_DECODER_2_out_5),
    .out_6(BCD_to_7_segment_DECODER_2_out_6), .out_7(BCD_to_7_segment_DECODER_2_out_7),
    .out_8(BCD_to_7_segment_DECODER_2_out_8), .out_9(BCD_to_7_segment_DECODER_2_out_9),
    .out_10(BCD_to_7_segment_DECODER_2_out_10), .out_11(BCD_to_7_segment_DECODER_2_out_11));
  _7_Segment_Display u_7_segment_display_2 (
    .g(BCD_to_7_segment_DECODER_2_out_11), .f(BCD_to_7_segment_DECODER_2_out_10),
    .a(BCD_to_7_segment_DECODER_2_out_5), .b(BCD_to_7_segment_DECODER_2_out_6),
    .e(BCD_to_7_segment_DECODER_2_out_9), .d(BCD_to_7_segment_DECODER_2_out_8),
    .c(BCD_to_7_segment_DECODER_2_out_7));  // open: dp
  Clock clock_3 (.out(clock_3_out));
  _4_bit_D_flip_flop D_flip_flop_3 (
    .CLK(clock_3_out), .LSB(in_7[0]), .in_3(in_7[1]), .in_4(in_7[2]), .MSB(in_7[3]),
    .LSB_2(D_flip_flop_3_lsb_2[0]), .out_7(D_flip_flop_3_lsb_2[1]), .out_8(D_flip_flop_3_lsb_2[2]),
    .MSB_2(D_flip_flop_3_lsb_2[3]));
  Clock clock_4 (.out(clock_4_out));
  BCD_to_7_segment_display BCD_to_7_segment_DECODER_3 (
    .MSB(_8_bit_binary_to_BCD_u3), .in_2(_8_bit_binary_to_BCD_u2), .in_3(_8_bit_binary_to_BCD_u1),
    .LSB(_8_bit_binary_to_BCD_u0), .out_5(BCD_to_7_segment_DECODER_3_out_5),
    .out_6(BCD_to_7_segment_DECODER_3_out_6), .out_7(BCD_to_7_segment_DECODER_3_out_7),
    .out_8(BCD_to_7_segment_DECODER_3_out_8), .out_9(BCD_to_7_segment_DECODER_3_out_9),
    .out_10(BCD_to_7_segment_DECODER_3_out_10), .out_11(BCD_to_7_segment_DECODER_3_out_11));
  _4_bit_D_flip_flop D_flip_flop_4 (
    .CLK(clock_4_out), .LSB(in_8[0]), .in_3(in_8[1]), .in_4(in_8[2]), .MSB(in_8[3]),
    .LSB_2(D_flip_flop_4_lsb_2[0]), .out_7(D_flip_flop_4_lsb_2[1]), .out_8(D_flip_flop_4_lsb_2[2]),
    .MSB_2(D_flip_flop_4_lsb_2[3]));
  _7_Segment_Display u_7_segment_display_3 (
    .g(BCD_to_7_segment_DECODER_3_out_11), .f(BCD_to_7_segment_DECODER_3_out_10),
    .a(BCD_to_7_segment_DECODER_3_out_5), .b(BCD_to_7_segment_DECODER_3_out_6),
    .e(BCD_to_7_segment_DECODER_3_out_9), .d(BCD_to_7_segment_DECODER_3_out_8),
    .c(BCD_to_7_segment_DECODER_3_out_7));  // open: dp
  comparator COMPARATOR (
    .less_than(COMPARATOR_less_than), .equal(COMPARATOR_equal), .in_2(D_flip_flop_4_lsb_2),
    .in_1(D_flip_flop_2_lsb_2));
  comparator COMPARATOR_2 (
    .less_than(COMPARATOR_2_less_than), .equal(COMPARATOR_2_equal), .in_2(D_flip_flop_3_lsb_2),
    .in_1(D_flip_flop_2_lsb_2));
  or or_1 (or_1_out, COMPARATOR_2_less_than, COMPARATOR_2_equal);
  or or_2 (or_2_out, COMPARATOR_less_than, COMPARATOR_equal);
  not not_1 (not_1_out, or_2_out);
  LED LED1 (.in(and_1_out));
  and and_1 (and_1_out, or_1_out, not_1_out);
  LED LED2 (.in(or_2_out));

  // Notes on the sheet:
  //   FUEL CONSUMED FOR OTHER CONSUMPTIONS (L/Km)  
  //   REMAINING FUEL
  //   MAXIMUM RANGE DISPLAYER
  //   5.) ENTER THE DISTANCE TRAVELLED
  //   2.) ON THE BASIS OF THESE INPUTS , MILEAGE WILL BE CALCULATED
  //   3.) ENTER THE AMOUNT OF FUEL IN YOUR VEHICLE
  //   TEAM ID:
  //   CHETAN KUMAR SAH 231CS102
  //   GIRISH SHARMA 231CS123
  //   INSTRUCTIONS
  //   ROAD QUALITY: 
  //   DRIVER'S QUALITY:
  //   TYPE OF VEHICLE:
  //   4.) MAXIMUM RANGE WILL BE DISPLAYED OB THE BASIS OF MILEAGE AND FUEL INPUT
  //   DIGITAL FUEL GAUGE WITH ADVANCED MONITORING FEATURES
  //   1.) SELECT ROAD QUALITY, DRIVER'S QUALITY AND VEHICLE TYPE ACCORDING TO ABOVE GIVEN INFORMATION
  //   6.) IT WILL CALCULATE THE REMAINING FUEL AND DISPLAY THE MAXIMUM RANGE ON THE BASIS OF REMAINING FUEL
  //   7.) LED'S WILL GLOW IF REMAINING FUEL BECOMES LESS THAN THRESHOLD OR MINIMUM THRESHOLD FUEL VALUE
  //   00 FOR INTERNATIONAL HIGHWAY
  //   01 FOR NATIONAL HIGHWAY
  //   10 FOR CITY ROAD
  //   11 FOR COUNTRYSIDE ROAD
  //   0 FOR EXPERT DRIVER
  //   1 FOR BEGINEER
  //   00 FOR MOTORBIKE
  //   01 FOR CAR (SEDAN)
  //   10 FOR CAR (SUV)
  //   11 FOR TRUCK
endmodule

module _4_bit_full_adder (
  input  CIN,
  input  A3,
  input  B3,
  input  A2,
  input  B2,
  input  A1,
  input  B1,
  input  A0,
  input  B0,
  output S3,
  output S2,
  output S1,
  output S0,
  output COUT
);

  wire adder_1_cout, adder_2_cout, adder_3_cout;

  Adder #(.width(1)) adder_1 (.a(A3), .b(B3), .out(S3), .cin(CIN), .cout(adder_1_cout));
  Adder #(.width(1)) adder_2 (.a(A2), .b(B2), .out(S2), .cin(adder_1_cout), .cout(adder_2_cout));
  Adder #(.width(1)) adder_3 (.a(A1), .b(B1), .out(S1), .cin(adder_2_cout), .cout(adder_3_cout));
  Adder #(.width(1)) adder_4 (.a(A0), .b(B0), .out(S0), .cin(adder_3_cout), .cout(COUT));
endmodule

module _5_bit_full_adder (
  input  CIN,
  input  A0,
  input  B0,
  input  A1,
  input  B1,
  input  A2,
  input  B2,
  input  A3,
  input  B3,
  input  A4,
  input  B4,
  output S0,
  output S1,
  output S2,
  output S3,
  output S4,
  output COUT
);

  wire adder_1_cout, adder_2_cout, adder_3_cout, adder_4_cout;

  Adder #(.width(1)) adder_1 (.a(A0), .b(B0), .out(S0), .cin(CIN), .cout(adder_1_cout));
  Adder #(.width(1)) adder_2 (.a(A1), .b(B1), .out(S1), .cin(adder_1_cout), .cout(adder_2_cout));
  Adder #(.width(1)) adder_3 (.a(A2), .b(B2), .out(S2), .cin(adder_2_cout), .cout(adder_3_cout));
  Adder #(.width(1)) adder_4 (.a(A3), .b(B3), .out(S3), .cin(adder_3_cout), .cout(adder_4_cout));
  Adder #(.width(1)) adder_5 (.a(A4), .b(B4), .out(S4), .cin(adder_4_cout), .cout(COUT));
endmodule

// MILEAGE
module mileage (
  input  in_1,
  input  in_2,
  input  in_3,
  input  in_4,
  input  in_5,
  input  in_6,
  input  in_7,
  input  in_8,
  input  in_9,
  input  in_10,
  input  in_11,
  input  in_12,
  input  in_13,
  output [5:0] out_14
);

  wire n4_bit_full_adder_1_cout, n4_bit_full_adder_1_s0, n4_bit_full_adder_1_s1, n4_bit_full_adder_1_s2,
       n4_bit_full_adder_1_s3;
  wire [5:0] n5_bit_full_adder_1_s0;

  _4_bit_full_adder u_4_bit_full_adder_1 (
    .A3(in_1), .B3(in_2), .A2(in_3), .B2(in_4), .A1(in_5), .B1(in_6), .A0(in_7), .B0(in_8),
    .S3(n4_bit_full_adder_1_s3), .S2(n4_bit_full_adder_1_s2), .S1(n4_bit_full_adder_1_s1),
    .S0(n4_bit_full_adder_1_s0), .COUT(n4_bit_full_adder_1_cout));  // open: CIN
  _5_bit_full_adder u_5_bit_full_adder_1 (
    .A0(n4_bit_full_adder_1_s3), .B0(in_9), .A1(n4_bit_full_adder_1_s2), .B1(in_10),
    .A2(n4_bit_full_adder_1_s1), .B2(in_11), .A3(n4_bit_full_adder_1_s0), .B3(in_12),
    .A4(n4_bit_full_adder_1_cout), .B4(in_13), .S0(n5_bit_full_adder_1_s0[0]),
    .S1(n5_bit_full_adder_1_s0[1]), .S2(n5_bit_full_adder_1_s0[2]), .S3(n5_bit_full_adder_1_s0[3]),
    .S4(n5_bit_full_adder_1_s0[4]), .COUT(n5_bit_full_adder_1_s0[5]));  // open: CIN
  Divider #(.width(6)) divider_1 (.a(n5_bit_full_adder_1_s0), .b(6'b000011), .out(out_14));  // open: upper, rem
endmodule

module _4_bit_multiplier (
  input  in_1,
  input  in_2,
  input  in_3,
  input  in_4,
  input  in_5,
  input  in_6,
  input  in_7,
  input  in_8,
  output [7:0] out_9
);

  wire [2:0] and_14_out;
  wire [3:0] adder_1_cout, adder_2_out, and_6_out, and_8_out, and_11_out;

  and and_1 (and_6_out[3], in_7, in_4);
  and and_2 (and_6_out[1], in_7, in_2);
  and and_3 (and_6_out[2], in_7, in_3);
  and and_4 (and_8_out[3], in_4, in_8);
  and and_5 (and_8_out[2], in_8, in_3);
  and and_6 (and_6_out[0], in_7, in_1);
  and and_7 (and_8_out[1], in_8, in_2);
  and and_8 (and_8_out[0], in_8, in_1);
  and and_9 (and_11_out[3], in_6, in_4);
  and and_10 (and_11_out[2], in_6, in_3);
  and and_11 (and_11_out[0], in_6, in_1);
  and and_12 (and_11_out[1], in_6, in_2);
  and and_13 (and_14_out[2], in_5, in_4);
  and and_14 (and_14_out[0], in_5, in_2);
  and and_15 (and_14_out[1], in_5, in_3);
  and and_16 (out_9[0], in_5, in_1);
  Adder #(.width(4)) adder_1 (
    .a({1'b0, and_14_out}), .b(and_11_out), .out({adder_1_cout[2:0], out_9[1]}), .cin(1'b0),
    .cout(adder_1_cout[3]));
  Adder #(.width(4)) adder_2 (
    .a(adder_1_cout), .b(and_6_out), .out({adder_2_out[2:0], out_9[2]}), .cin(1'b0), .cout(adder_2_out[3]));
  Adder #(.width(4)) adder_3 (.a(adder_2_out), .b(and_8_out), .out(out_9[6:3]), .cin(1'b0), .cout(out_9[7]));
endmodule

module _8_bit_binary_to_BCD (
  input  A,
  input  B,
  input  C,
  input  D,
  input  E,
  input  F,
  input  G,
  input  H,
  output H3,
  output H2,
  output H1,
  output H0,
  output T3,
  output T2,
  output T1,
  output T0,
  output U3,
  output U2,
  output U1,
  output U0
);

  wire and_1_out, and_2_out, and_3_out, and_4_out, and_5_out, and_6_out, and_7_out, and_8_out, and_9_out,
       and_10_out, and_11_out, and_12_out, and_13_out, and_14_out, and_15_out, and_16_out, and_17_out,
       and_18_out, and_19_out, and_20_out, and_21_out, and_22_out, and_23_out, and_24_out, and_25_out,
       and_26_out, and_27_out, and_28_out, and_29_out, and_30_out, and_31_out, and_32_out, and_33_out,
       and_34_out, and_35_out, and_36_out, and_37_out, and_38_out, and_39_out, and_40_out, and_41_out,
       and_42_out, and_43_out, and_44_out, and_45_out, and_46_out, and_47_out, and_48_out, and_49_out,
       and_50_out, and_51_out, and_52_out, and_53_out, and_54_out, and_55_out, and_56_out, and_57_out,
       and_58_out, and_59_out, and_60_out, and_61_out, and_62_out, and_63_out, and_64_out, and_65_out,
       and_66_out, and_67_out, and_68_out, and_69_out, and_70_out, and_71_out, and_72_out, and_73_out,
       and_74_out, and_75_out, and_76_out, and_77_out, and_78_out, and_79_out, and_80_out, and_81_out,
       and_82_out, and_83_out, and_84_out, and_85_out, and_86_out, and_87_out, and_88_out, and_89_out,
       and_90_out, and_91_out, and_92_out, and_93_out, and_94_out, and_95_out, and_96_out, and_97_out,
       and_98_out, and_99_out, and_100_out, and_101_out, and_102_out, and_103_out, and_104_out, and_105_out,
       and_106_out, and_107_out, and_108_out, and_109_out, and_110_out, and_111_out, and_112_out,
       and_113_out, and_114_out, and_115_out, and_116_out, and_117_out, and_118_out, and_119_out,
       and_120_out, and_121_out, and_122_out, and_123_out, and_124_out, and_125_out, and_126_out,
       and_127_out, and_128_out, and_129_out, and_130_out, and_131_out, and_132_out, and_133_out,
       and_134_out, and_135_out, and_136_out, and_137_out, and_138_out, and_139_out, and_140_out,
       and_141_out, and_142_out, and_143_out, and_144_out, and_145_out, and_146_out, and_147_out,
       and_148_out, and_149_out, and_150_out, and_151_out, and_152_out, and_153_out, and_154_out,
       and_155_out, and_156_out, and_157_out, and_158_out, and_159_out, and_160_out, and_161_out,
       and_162_out, and_163_out, and_164_out, and_165_out, and_166_out, and_167_out, and_168_out,
       and_169_out, and_170_out, and_171_out, and_172_out, and_173_out, and_174_out, and_175_out,
       and_176_out, and_177_out, and_178_out, and_179_out, and_180_out, and_181_out, and_182_out,
       and_183_out, and_184_out, and_185_out, and_186_out, and_187_out, and_188_out, and_189_out,
       and_190_out, and_191_out, and_192_out, and_193_out, and_194_out, and_195_out, and_196_out,
       and_197_out, and_198_out, and_199_out, and_200_out, and_201_out, and_202_out, and_203_out,
       and_204_out, and_205_out, and_206_out, and_207_out, and_208_out, and_209_out, and_210_out,
       and_211_out, and_212_out, and_213_out, and_214_out, and_215_out, and_216_out, and_217_out,
       and_218_out, and_219_out, and_220_out, and_221_out, and_222_out, and_223_out, and_224_out,
       and_225_out, and_226_out, and_227_out, and_228_out, and_229_out, and_230_out, and_231_out,
       and_232_out, and_233_out, and_234_out, and_235_out, and_236_out, and_237_out, and_238_out,
       and_239_out, and_240_out, and_241_out, and_242_out, and_243_out, and_244_out, and_245_out,
       and_246_out, and_247_out, and_248_out, and_249_out, and_250_out, and_251_out, and_252_out,
       and_253_out, and_254_out, and_255_out, and_256_out, and_257_out, and_258_out, and_259_out,
       and_260_out, and_261_out, and_262_out, and_263_out, and_264_out, and_265_out, and_266_out,
       and_267_out, and_268_out, and_269_out, and_270_out, and_271_out, and_272_out, and_273_out,
       and_274_out, and_275_out, and_276_out, and_277_out, and_278_out, and_279_out, and_280_out,
       and_281_out, and_282_out, and_283_out, and_284_out, and_285_out, and_286_out, and_287_out,
       and_288_out, and_289_out, and_290_out, and_291_out, and_292_out, and_293_out, and_294_out,
       and_295_out, and_296_out, and_297_out, and_298_out, and_299_out, and_300_out, and_301_out,
       and_302_out, and_303_out, and_304_out, and_305_out, and_306_out, and_307_out, and_308_out,
       and_309_out, and_310_out, and_311_out, and_312_out, and_313_out, and_314_out, and_315_out,
       and_316_out, and_317_out, and_318_out, and_319_out, and_320_out, and_321_out, and_322_out,
       and_323_out, and_324_out, and_325_out, and_326_out, and_327_out, and_328_out, and_329_out,
       and_330_out, and_331_out, and_332_out, and_333_out, and_334_out, and_335_out, and_336_out,
       and_337_out, and_338_out, and_339_out, and_340_out, and_341_out, and_342_out, and_343_out,
       and_344_out, and_345_out, and_346_out, and_347_out, and_348_out, and_349_out, and_350_out,
       and_351_out, and_352_out, and_353_out, and_354_out, and_355_out, and_356_out, and_357_out,
       and_358_out, and_359_out, and_360_out, and_361_out, and_362_out, and_363_out, and_364_out,
       and_365_out, and_366_out, and_367_out, and_368_out, and_369_out, and_370_out, and_371_out,
       and_372_out, and_373_out, and_374_out, and_375_out, and_376_out, and_377_out, and_378_out,
       and_379_out, and_380_out, and_381_out, and_382_out, and_383_out, and_384_out, and_385_out,
       and_386_out, and_387_out, and_388_out, and_389_out, and_390_out, and_391_out, and_392_out,
       and_393_out, and_394_out, and_395_out, and_396_out, and_397_out, and_398_out, and_399_out,
       and_400_out, and_401_out, and_402_out, and_403_out, and_404_out, and_405_out, and_406_out,
       and_407_out, and_408_out, and_409_out, and_410_out, and_411_out, and_412_out, and_413_out,
       and_414_out, and_415_out, and_416_out, and_417_out, and_418_out, and_419_out, and_420_out,
       and_421_out, and_422_out, and_423_out, and_424_out, and_425_out, and_426_out, and_427_out,
       and_428_out, and_429_out, and_430_out, and_431_out, and_432_out, and_433_out, and_434_out,
       and_435_out, and_436_out, and_437_out, and_438_out, and_439_out, and_440_out, and_441_out,
       and_442_out, and_443_out, and_444_out, and_445_out, and_446_out, and_447_out, and_448_out,
       and_449_out, and_450_out, and_451_out, and_452_out, and_453_out, and_454_out, and_455_out,
       and_456_out, and_457_out, and_458_out, and_459_out, and_460_out, and_461_out, and_462_out,
       and_463_out, and_464_out, and_465_out, and_466_out, and_467_out, and_468_out, and_469_out,
       and_470_out, and_471_out, and_472_out, and_473_out, and_474_out, and_475_out, and_476_out,
       and_477_out, and_478_out, and_479_out, and_480_out, and_481_out, and_482_out, and_483_out,
       and_484_out, and_485_out, and_486_out, and_487_out, and_488_out, and_489_out, and_490_out,
       and_491_out, and_492_out, and_493_out, and_494_out, and_495_out, and_496_out, and_497_out,
       and_498_out, and_499_out, and_500_out, and_501_out, and_502_out, and_503_out, and_504_out,
       and_505_out, and_506_out, and_507_out, and_508_out, and_509_out, and_510_out, and_511_out,
       and_512_out, and_513_out, and_514_out, and_515_out, and_516_out, and_517_out, and_518_out,
       and_519_out, and_520_out, and_521_out, and_522_out, and_523_out, and_524_out, and_525_out,
       and_526_out, and_527_out, and_528_out, and_529_out, and_530_out, and_531_out, and_532_out,
       and_533_out, and_534_out, and_535_out, and_536_out, and_537_out, and_538_out, and_539_out,
       and_540_out, and_541_out, and_542_out, and_543_out, and_544_out, and_545_out, and_546_out,
       and_547_out, and_548_out, and_549_out, and_550_out, and_551_out, and_552_out, and_553_out,
       and_554_out, and_555_out, and_556_out, and_557_out, and_558_out, and_559_out, and_560_out,
       and_561_out, and_562_out, and_563_out, and_564_out, and_565_out, and_566_out, and_567_out,
       and_568_out, and_569_out, and_570_out, and_571_out, and_572_out, and_573_out, and_574_out,
       and_575_out, and_576_out, and_577_out, and_578_out, and_579_out, and_580_out, and_581_out,
       and_582_out, and_583_out, and_584_out, and_585_out, and_586_out, and_587_out, and_588_out,
       and_589_out, and_590_out, and_591_out, and_592_out, and_593_out, and_594_out, and_595_out,
       and_596_out, and_597_out, and_598_out, and_599_out, and_600_out, and_601_out, and_602_out,
       and_603_out, and_604_out, and_605_out, and_606_out, and_607_out, and_608_out, and_609_out,
       and_610_out, and_611_out, and_612_out, and_613_out, and_614_out, and_615_out, and_616_out,
       and_617_out, and_618_out, and_619_out, and_620_out, and_621_out, and_622_out, and_623_out,
       and_624_out, and_625_out, and_626_out, and_627_out, and_628_out, and_629_out, and_630_out,
       and_631_out, and_632_out, and_633_out, and_634_out, and_635_out, and_636_out, and_637_out,
       and_638_out, and_639_out, and_640_out, and_641_out, and_642_out, and_643_out, and_644_out,
       and_645_out, and_646_out, and_647_out, and_648_out, and_649_out, and_650_out, and_651_out,
       and_652_out, and_653_out, and_654_out, and_655_out, and_656_out, and_657_out, and_658_out,
       and_659_out, and_660_out, and_661_out, and_662_out, and_663_out, and_664_out, and_665_out,
       and_666_out, and_667_out, and_668_out, and_669_out, and_670_out, and_671_out, and_672_out,
       and_673_out, and_674_out, and_675_out, and_676_out, and_677_out, and_678_out, and_679_out,
       and_680_out, and_681_out, and_682_out, and_683_out, and_684_out, and_685_out, and_686_out,
       and_687_out, and_688_out, and_689_out, and_690_out, and_691_out, and_692_out, and_693_out,
       and_694_out, and_695_out, and_696_out, and_697_out, and_698_out, and_699_out, and_700_out,
       and_701_out, and_702_out, and_703_out, and_704_out, and_705_out, and_706_out, and_707_out,
       and_708_out, and_709_out, and_710_out, and_711_out, and_712_out, and_713_out, and_714_out,
       and_715_out, and_716_out, and_717_out, and_718_out, and_719_out, and_720_out, and_721_out,
       and_722_out, and_723_out, and_724_out, and_725_out, and_726_out, and_727_out, and_728_out,
       and_729_out, and_730_out, and_731_out, and_732_out, and_733_out, and_734_out, and_735_out,
       and_736_out, and_737_out, not_1_out, not_2_out, not_3_out, not_4_out, not_5_out, not_6_out, not_7_out,
       not_8_out, not_9_out, not_10_out, not_11_out, not_12_out, not_13_out, not_14_out, not_15_out,
       not_16_out, not_17_out, not_18_out, not_19_out, not_20_out, not_21_out, not_22_out, not_23_out,
       not_24_out, not_25_out, not_26_out, not_27_out, not_28_out, not_29_out, not_30_out, not_31_out,
       not_32_out, not_33_out, not_34_out, not_35_out, not_36_out, not_37_out, not_38_out, not_39_out,
       not_40_out, not_41_out, not_42_out, not_43_out, not_44_out, not_45_out, not_46_out, not_47_out,
       not_48_out, not_49_out, not_50_out, not_51_out, not_52_out, not_53_out, not_54_out, not_55_out,
       not_56_out, not_57_out, not_58_out, not_59_out, not_60_out, not_61_out, not_62_out, not_63_out,
       not_64_out, not_65_out, not_66_out, not_67_out, not_68_out, not_69_out, not_70_out, not_71_out,
       not_72_out, not_73_out, not_74_out, not_75_out, not_76_out, not_77_out, not_78_out, not_79_out,
       not_80_out, not_81_out, not_82_out, not_83_out, not_84_out, not_85_out, not_86_out, not_87_out,
       not_88_out, not_89_out, not_90_out, not_91_out, not_92_out, not_93_out, not_94_out, not_95_out,
       not_96_out, not_97_out, not_98_out, not_99_out, not_100_out, not_101_out, not_102_out, not_103_out,
       not_104_out, not_105_out, not_106_out, not_107_out, not_108_out, not_109_out, not_110_out,
       not_111_out, not_112_out, not_113_out, not_114_out, not_115_out, not_116_out, not_117_out,
       not_118_out, not_119_out, not_120_out, not_121_out, not_122_out, not_123_out, not_124_out,
       not_125_out, not_126_out, not_127_out, not_128_out, not_129_out, not_130_out, not_131_out,
       not_132_out, not_133_out, not_134_out, not_135_out, not_136_out, not_137_out, not_138_out,
       not_139_out, not_140_out, not_141_out, not_142_out, not_143_out, not_144_out, not_145_out,
       not_146_out, not_147_out, not_148_out, not_149_out, not_150_out, not_151_out, not_152_out,
       not_153_out, not_154_out, not_155_out, not_156_out, not_157_out, not_158_out, not_159_out,
       not_160_out, not_161_out, not_162_out, not_163_out, not_164_out, not_165_out, not_166_out,
       not_167_out, not_168_out, not_169_out, not_170_out, not_171_out, not_172_out, not_173_out,
       not_174_out, not_175_out, not_176_out, not_177_out, not_178_out, not_179_out, not_180_out,
       not_181_out, not_182_out, not_183_out, not_184_out, not_185_out, not_186_out, not_187_out,
       not_188_out, not_189_out, not_190_out, not_191_out, not_192_out, not_193_out, not_194_out,
       not_195_out, not_196_out, not_197_out, not_198_out, not_199_out, not_200_out, not_201_out,
       not_202_out, not_203_out, not_204_out, not_205_out, not_206_out, not_207_out, not_208_out,
       not_209_out, not_210_out, not_211_out, not_212_out, not_213_out, not_214_out, not_215_out,
       not_216_out, not_217_out, not_218_out, not_219_out, not_220_out, not_221_out, not_222_out,
       not_223_out, not_224_out, not_225_out, not_226_out, not_227_out, not_228_out, not_229_out,
       not_230_out, not_231_out, not_232_out, not_233_out, not_234_out, not_235_out, not_236_out,
       not_237_out, not_238_out, not_239_out, not_240_out, not_241_out, not_242_out, not_243_out,
       not_244_out, not_245_out, not_246_out, not_247_out, not_248_out, not_249_out, not_250_out,
       not_251_out, not_252_out, not_253_out, not_254_out, not_255_out, not_256_out, not_257_out,
       not_258_out, not_259_out, not_260_out, not_261_out, not_262_out, not_263_out, not_264_out,
       not_265_out, not_266_out, not_267_out, not_268_out, not_269_out, not_270_out, not_271_out,
       not_272_out, not_273_out, not_274_out, not_275_out, not_276_out, not_277_out, not_278_out,
       not_279_out, not_280_out, not_281_out, not_282_out, not_283_out, not_284_out, not_285_out,
       not_286_out, not_287_out, not_288_out, not_289_out, not_290_out, not_291_out, not_292_out,
       not_293_out, not_294_out, not_295_out, not_296_out, not_297_out, not_298_out, not_299_out,
       not_300_out, not_301_out, not_302_out, not_303_out, not_304_out, not_305_out, not_306_out,
       not_307_out, not_308_out, not_309_out, not_310_out, not_311_out, not_312_out, not_313_out,
       not_314_out, not_315_out, not_316_out, not_317_out, not_318_out, not_319_out, not_320_out,
       not_321_out, not_322_out, not_323_out, not_324_out, not_325_out, not_326_out, not_327_out,
       not_328_out, not_329_out, not_330_out, not_331_out, not_332_out, not_333_out, not_334_out,
       not_335_out, not_336_out, not_337_out, not_338_out, not_339_out, not_340_out, not_341_out,
       not_342_out, not_343_out, not_344_out, not_345_out, not_346_out, not_347_out, not_348_out,
       not_349_out, not_350_out, not_351_out, not_352_out, not_353_out, not_354_out, not_355_out,
       not_356_out, not_357_out, not_358_out, not_359_out, not_360_out, not_361_out, not_362_out,
       not_363_out, not_364_out, not_365_out, not_366_out, not_367_out, not_368_out, not_369_out,
       not_370_out, not_371_out, not_372_out, not_373_out, not_374_out, not_375_out, not_376_out,
       not_377_out, not_378_out, not_379_out, not_380_out, not_381_out, not_382_out, not_383_out,
       not_384_out, not_385_out, not_386_out, not_387_out, not_388_out, not_389_out, not_390_out,
       not_391_out, not_392_out, not_393_out, not_394_out, not_395_out, not_396_out, not_397_out,
       not_398_out, not_399_out, not_400_out, not_401_out, not_402_out, not_403_out, not_404_out,
       not_405_out, not_406_out, not_407_out, not_408_out, not_409_out, not_410_out, not_411_out,
       not_412_out, not_413_out, not_414_out, not_415_out, not_416_out, not_417_out, not_418_out,
       not_419_out, not_420_out, not_421_out, not_422_out, not_423_out, not_424_out, not_425_out,
       not_426_out, not_427_out, or_1_out, or_3_out, or_4_out, or_5_out, or_6_out, or_7_out, or_8_out,
       or_9_out, or_10_out, or_11_out, or_12_out, or_13_out, or_14_out, or_15_out, or_16_out, or_17_out,
       or_18_out, or_19_out, or_20_out, or_21_out, or_22_out, or_23_out, or_24_out, or_25_out, or_26_out,
       or_27_out, or_28_out, or_29_out, or_30_out, or_31_out, or_32_out, or_33_out, or_34_out, or_35_out,
       or_36_out, or_37_out, or_38_out, or_39_out, or_40_out, or_41_out, or_43_out, or_44_out, or_45_out,
       or_46_out, or_47_out, or_48_out, or_49_out, or_50_out, or_51_out, or_52_out, or_53_out, or_54_out,
       or_55_out, or_56_out, or_57_out, or_58_out, or_59_out, or_60_out, or_61_out, or_62_out, or_63_out,
       or_64_out, or_65_out, or_66_out, or_67_out, or_68_out, or_69_out, or_70_out, or_71_out, or_72_out,
       or_73_out, or_74_out, or_75_out, or_76_out, or_77_out, or_78_out, or_79_out, or_80_out, or_81_out,
       or_82_out, or_83_out, or_84_out, or_85_out, or_86_out, or_87_out, or_88_out, or_89_out, or_90_out,
       or_91_out, or_92_out, or_93_out, or_94_out, or_95_out, or_96_out, or_97_out, or_98_out, or_101_out,
       or_102_out, or_103_out, or_104_out, or_105_out, or_106_out, or_107_out, or_108_out, or_109_out,
       or_110_out, or_111_out, or_112_out, or_113_out, or_114_out, or_115_out, or_116_out, or_117_out,
       or_118_out, or_119_out, or_120_out, or_121_out, or_122_out, or_123_out, or_124_out, or_125_out,
       or_126_out, or_128_out, or_129_out, or_130_out, or_131_out, or_132_out, or_133_out, or_134_out,
       or_135_out, or_136_out, or_137_out, or_138_out, or_139_out, or_142_out, or_144_out, or_145_out,
       or_147_out;

  and and_1 (and_1_out, A, B);
  and and_2 (and_2_out, A, B);
  not not_1 (not_1_out, A);
  and and_3 (and_3_out, not_1_out, B);
  and and_4 (and_4_out, C, F);
  not not_2 (not_2_out, A);
  and and_5 (and_5_out, not_2_out, B);
  and and_6 (and_6_out, C, E);
  not not_3 (not_3_out, A);
  not not_4 (not_4_out, C);
  not not_5 (not_5_out, D);
  not not_6 (not_6_out, E);
  not not_7 (not_7_out, A);
  not not_8 (not_8_out, C);
  not not_9 (not_9_out, A);
  and and_7 (and_7_out, not_9_out, B);
  not not_10 (not_10_out, D);
  and and_8 (and_8_out, not_10_out, not_11_out);
  not not_11 (not_11_out, E);
  not not_12 (not_12_out, F);
  not not_13 (not_13_out, B);
  not not_14 (not_14_out, B);
  not not_15 (not_15_out, B);
  not not_16 (not_16_out, D);
  not not_17 (not_17_out, A);
  not not_18 (not_18_out, B);
  not not_19 (not_19_out, A);
  not not_20 (not_20_out, C);
  not not_21 (not_21_out, D);
  and and_9 (and_9_out, A, not_22_out);
  not not_22 (not_22_out, B);
  not not_23 (not_23_out, D);
  not not_24 (not_24_out, B);
  not not_25 (not_25_out, C);
  not not_26 (not_26_out, B);
  not not_27 (not_27_out, D);
  and and_10 (and_10_out, A, not_28_out);
  not not_28 (not_28_out, B);
  not not_29 (not_29_out, E);
  not not_30 (not_30_out, F);
  not not_31 (not_31_out, A);
  and and_11 (and_11_out, not_31_out, not_32_out);
  not not_32 (not_32_out, B);
  not not_33 (not_33_out, C);
  not not_34 (not_34_out, A);
  and and_12 (and_12_out, not_34_out, not_35_out);
  not not_35 (not_35_out, B);
  not not_36 (not_36_out, C);
  not not_37 (not_37_out, A);
  not not_38 (not_38_out, B);
  not not_39 (not_39_out, B);
  not not_40 (not_40_out, D);
  not not_41 (not_41_out, E);
  not not_42 (not_42_out, A);
  not not_43 (not_43_out, C);
  not not_44 (not_44_out, D);
  not not_45 (not_45_out, A);
  not not_46 (not_46_out, B);
  not not_47 (not_47_out, D);
  not not_48 (not_48_out, E);
  not not_49 (not_49_out, B);
  not not_50 (not_50_out, D);
  not not_51 (not_51_out, F);
  not not_52 (not_52_out, B);
  not not_53 (not_53_out, A);
  and and_13 (and_13_out, not_53_out, not_54_out);
  not not_54 (not_54_out, C);
  not not_55 (not_55_out, D);
  not not_56 (not_56_out, A);
  and and_14 (and_14_out, not_56_out, not_57_out);
  not not_57 (not_57_out, C);
  not not_58 (not_58_out, D);
  not not_59 (not_59_out, A);
  and and_15 (and_15_out, not_59_out, not_60_out);
  not not_60 (not_60_out, C);
  not not_61 (not_61_out, A);
  and and_16 (and_16_out, not_61_out, not_62_out);
  not not_62 (not_62_out, B);
  not not_63 (not_63_out, C);
  and and_17 (and_17_out, D, not_64_out);
  not not_64 (not_64_out, E);
  not not_65 (not_65_out, F);
  not not_66 (not_66_out, A);
  and and_18 (and_18_out, not_66_out, not_67_out);
  not not_67 (not_67_out, B);
  not not_68 (not_68_out, D);
  not not_69 (not_69_out, E);
  not not_70 (not_70_out, A);
  and and_19 (and_19_out, not_70_out, not_71_out);
  not not_71 (not_71_out, B);
  not not_72 (not_72_out, E);
  not not_73 (not_73_out, A);
  and and_20 (and_20_out, not_73_out, C);
  not not_74 (not_74_out, E);
  not not_75 (not_75_out, A);
  and and_21 (and_21_out, not_75_out, not_76_out);
  not not_76 (not_76_out, B);
  and and_22 (and_22_out, D, E);
  not not_77 (not_77_out, F);
  and and_23 (and_23_out, B, not_78_out);
  not not_78 (not_78_out, C);
  not not_79 (not_79_out, D);
  not not_80 (not_80_out, E);
  and and_24 (and_24_out, not_80_out, F);
  not not_81 (not_81_out, A);
  and and_25 (and_25_out, not_81_out, B);
  not not_82 (not_82_out, C);
  not not_83 (not_83_out, D);
  not not_84 (not_84_out, A);
  and and_26 (and_26_out, not_84_out, B);
  not not_85 (not_85_out, C);
  not not_86 (not_86_out, A);
  and and_27 (and_27_out, not_86_out, B);
  not not_87 (not_87_out, C);
  not not_88 (not_88_out, A);
  and and_28 (and_28_out, not_88_out, B);
  not not_89 (not_89_out, D);
  and and_29 (and_29_out, E, F);
  not not_90 (not_90_out, A);
  and and_30 (and_30_out, not_90_out, B);
  not not_91 (not_91_out, E);
  not not_92 (not_92_out, F);
  and and_31 (and_31_out, A, not_93_out);
  not not_93 (not_93_out, C);
  not not_94 (not_94_out, D);
  not not_95 (not_95_out, E);
  and and_32 (and_32_out, A, not_96_out);
  not not_96 (not_96_out, C);
  not not_97 (not_97_out, D);
  not not_98 (not_98_out, E);
  and and_33 (and_33_out, A, not_99_out);
  not not_99 (not_99_out, C);
  not not_100 (not_100_out, E);
  and and_34 (and_34_out, A, not_101_out);
  not not_101 (not_101_out, B);
  not not_102 (not_102_out, C);
  not not_103 (not_103_out, F);
  and and_35 (and_35_out, A, not_104_out);
  not not_104 (not_104_out, B);
  not not_105 (not_105_out, C);
  and and_36 (and_36_out, A, not_106_out);
  not not_106 (not_106_out, C);
  not not_107 (not_107_out, F);
  and and_37 (and_37_out, A, C);
  not not_108 (not_108_out, D);
  and and_38 (and_38_out, A, C);
  not not_109 (not_109_out, D);
  and and_39 (and_39_out, A, C);
  and and_40 (and_40_out, A, not_110_out);
  not not_110 (not_110_out, B);
  and and_41 (and_41_out, D, not_111_out);
  not not_111 (not_111_out, E);
  not not_112 (not_112_out, F);
  and and_42 (and_42_out, A, B);
  not not_113 (not_113_out, C);
  not not_114 (not_114_out, D);
  not not_115 (not_115_out, E);
  and and_43 (and_43_out, A, B);
  not not_116 (not_116_out, C);
  not not_117 (not_117_out, E);
  and and_44 (and_44_out, A, B);
  not not_118 (not_118_out, C);
  not not_119 (not_119_out, E);
  and and_45 (and_45_out, A, B);
  not not_120 (not_120_out, D);
  not not_121 (not_121_out, E);
  and and_46 (and_46_out, not_121_out, F);
  and and_47 (and_47_out, A, B);
  not not_122 (not_122_out, D);
  and and_48 (and_48_out, A, B);
  not not_123 (not_123_out, A);
  and and_49 (and_49_out, not_123_out, not_124_out);
  not not_124 (not_124_out, B);
  not not_125 (not_125_out, C);
  and and_50 (and_50_out, not_125_out, not_126_out);
  not not_126 (not_126_out, D);
  and and_51 (and_51_out, E, not_127_out);
  not not_127 (not_127_out, F);
  not not_128 (not_128_out, G);
  not not_129 (not_129_out, A);
  and and_52 (and_52_out, not_129_out, not_130_out);
  not not_130 (not_130_out, B);
  not not_131 (not_131_out, C);
  and and_53 (and_53_out, not_131_out, D);
  not not_132 (not_132_out, E);
  and and_54 (and_54_out, not_132_out, not_133_out);
  not not_133 (not_133_out, F);
  not not_134 (not_134_out, A);
  and and_55 (and_55_out, not_134_out, not_135_out);
  not not_135 (not_135_out, B);
  not not_136 (not_136_out, C);
  and and_56 (and_56_out, not_136_out, D);
  and and_57 (and_57_out, E, F);
  not not_137 (not_137_out, G);
  not not_138 (not_138_out, A);
  and and_58 (and_58_out, not_138_out, not_139_out);
  not not_139 (not_139_out, B);
  and and_59 (and_59_out, C, not_140_out);
  not not_140 (not_140_out, D);
  not not_141 (not_141_out, E);
  and and_60 (and_60_out, not_141_out, F);
  not not_142 (not_142_out, A);
  and and_61 (and_61_out, not_142_out, not_143_out);
  not not_143 (not_143_out, B);
  and and_62 (and_62_out, C, D);
  not not_144 (not_144_out, E);
  and and_63 (and_63_out, not_144_out, not_145_out);
  not not_145 (not_145_out, F);
  not not_146 (not_146_out, G);
  not not_147 (not_147_out, A);
  and and_64 (and_64_out, not_147_out, not_148_out);
  not not_148 (not_148_out, B);
  and and_65 (and_65_out, C, D);
  and and_66 (and_66_out, E, not_149_out);
  not not_149 (not_149_out, F);
  not not_150 (not_150_out, A);
  not not_151 (not_151_out, C);
  not not_152 (not_152_out, D);
  not not_153 (not_153_out, E);
  not not_154 (not_154_out, A);
  and and_67 (and_67_out, not_154_out, B);
  not not_155 (not_155_out, C);
  and and_68 (and_68_out, not_155_out, not_156_out);
  not not_156 (not_156_out, D);
  and and_69 (and_69_out, E, F);
  not not_157 (not_157_out, A);
  and and_70 (and_70_out, not_157_out, B);
  not not_158 (not_158_out, C);
  and and_71 (and_71_out, not_158_out, D);
  and and_72 (and_72_out, E, not_159_out);
  not not_159 (not_159_out, F);
  not not_160 (not_160_out, G);
  not not_161 (not_161_out, A);
  not not_162 (not_162_out, D);
  not not_163 (not_163_out, E);
  not not_164 (not_164_out, F);
  not not_165 (not_165_out, A);
  and and_73 (and_73_out, not_165_out, B);
  and and_74 (and_74_out, C, not_166_out);
  not not_166 (not_166_out, D);
  and and_75 (and_75_out, E, F);
  not not_167 (not_167_out, G);
  not not_168 (not_168_out, A);
  and and_76 (and_76_out, not_168_out, B);
  and and_77 (and_77_out, C, D);
  not not_169 (not_169_out, E);
  and and_78 (and_78_out, not_169_out, F);
  not not_170 (not_170_out, B);
  not not_171 (not_171_out, C);
  not not_172 (not_172_out, D);
  not not_173 (not_173_out, E);
  not not_174 (not_174_out, F);
  and and_79 (and_79_out, A, not_175_out);
  not not_175 (not_175_out, B);
  not not_176 (not_176_out, C);
  and and_80 (and_80_out, not_176_out, not_177_out);
  not not_177 (not_177_out, D);
  and and_81 (and_81_out, E, not_178_out);
  not not_178 (not_178_out, F);
  and and_82 (and_82_out, A, not_179_out);
  not not_179 (not_179_out, B);
  not not_180 (not_180_out, C);
  and and_83 (and_83_out, not_180_out, D);
  not not_181 (not_181_out, E);
  and and_84 (and_84_out, not_181_out, F);
  not not_182 (not_182_out, G);
  not not_183 (not_183_out, B);
  not not_184 (not_184_out, C);
  and and_85 (and_85_out, A, not_185_out);
  not not_185 (not_185_out, B);
  and and_86 (and_86_out, C, not_186_out);
  not not_186 (not_186_out, D);
  and and_87 (and_87_out, E, not_187_out);
  not not_187 (not_187_out, F);
  not not_188 (not_188_out, G);
  and and_88 (and_88_out, A, not_189_out);
  not not_189 (not_189_out, B);
  and and_89 (and_89_out, C, D);
  not not_190 (not_190_out, E);
  and and_90 (and_90_out, not_190_out, not_191_out);
  not not_191 (not_191_out, F);
  not not_192 (not_192_out, B);
  and and_91 (and_91_out, A, B);
  not not_193 (not_193_out, C);
  and and_92 (and_92_out, not_193_out, not_194_out);
  not not_194 (not_194_out, D);
  not not_195 (not_195_out, E);
  and and_93 (and_93_out, not_195_out, F);
  and and_94 (and_94_out, A, B);
  not not_196 (not_196_out, C);
  and and_95 (and_95_out, not_196_out, D);
  not not_197 (not_197_out, E);
  and and_96 (and_96_out, not_197_out, not_198_out);
  not not_198 (not_198_out, F);
  not not_199 (not_199_out, G);
  not not_200 (not_200_out, C);
  not not_201 (not_201_out, F);
  and and_97 (and_97_out, A, B);
  and and_98 (and_98_out, C, not_202_out);
  not not_202 (not_202_out, D);
  not not_203 (not_203_out, E);
  and and_99 (and_99_out, not_203_out, F);
  not not_204 (not_204_out, G);
  and and_100 (and_100_out, A, B);
  and and_101 (and_101_out, C, not_205_out);
  not not_205 (not_205_out, D);
  and and_102 (and_102_out, E, F);
  not not_206 (not_206_out, F);
  not not_207 (not_207_out, A);
  and and_103 (and_103_out, not_207_out, not_208_out);
  not not_208 (not_208_out, B);
  not not_209 (not_209_out, C);
  not not_210 (not_210_out, D);
  and and_104 (and_104_out, not_210_out, not_211_out);
  not not_211 (not_211_out, E);
  not not_212 (not_212_out, A);
  and and_105 (and_105_out, not_212_out, not_213_out);
  not not_213 (not_213_out, B);
  not not_214 (not_214_out, C);
  not not_215 (not_215_out, D);
  and and_106 (and_106_out, not_215_out, F);
  not not_216 (not_216_out, B);
  not not_217 (not_217_out, C);
  not not_218 (not_218_out, E);
  not not_219 (not_219_out, F);
  not not_220 (not_220_out, A);
  not not_221 (not_221_out, B);
  not not_222 (not_222_out, A);
  not not_223 (not_223_out, B);
  not not_224 (not_224_out, F);
  not not_225 (not_225_out, A);
  not not_226 (not_226_out, B);
  not not_227 (not_227_out, D);
  not not_228 (not_228_out, E);
  not not_229 (not_229_out, F);
  not not_230 (not_230_out, B);
  not not_231 (not_231_out, E);
  not not_232 (not_232_out, A);
  not not_233 (not_233_out, B);
  not not_234 (not_234_out, D);
  not not_235 (not_235_out, A);
  not not_236 (not_236_out, B);
  not not_237 (not_237_out, E);
  not not_238 (not_238_out, A);
  not not_239 (not_239_out, D);
  not not_240 (not_240_out, E);
  not not_241 (not_241_out, A);
  not not_242 (not_242_out, D);
  not not_243 (not_243_out, F);
  not not_244 (not_244_out, C);
  not not_245 (not_245_out, A);
  not not_246 (not_246_out, E);
  not not_247 (not_247_out, A);
  not not_248 (not_248_out, E);
  not not_249 (not_249_out, F);
  not not_250 (not_250_out, A);
  not not_251 (not_251_out, D);
  not not_252 (not_252_out, A);
  not not_253 (not_253_out, E);
  not not_254 (not_254_out, F);
  and and_107 (and_107_out, B, C);
  not not_255 (not_255_out, E);
  and and_108 (and_108_out, not_255_out, F);
  not not_256 (not_256_out, G);
  not not_257 (not_257_out, A);
  and and_109 (and_109_out, not_257_out, B);
  and and_110 (and_110_out, D, E);
  not not_258 (not_258_out, B);
  not not_259 (not_259_out, E);
  not not_260 (not_260_out, B);
  not not_261 (not_261_out, C);
  not not_262 (not_262_out, D);
  not not_263 (not_263_out, F);
  not not_264 (not_264_out, B);
  not not_265 (not_265_out, F);
  not not_266 (not_266_out, B);
  not not_267 (not_267_out, C);
  not not_268 (not_268_out, B);
  not not_269 (not_269_out, D);
  not not_270 (not_270_out, B);
  not not_271 (not_271_out, F);
  not not_272 (not_272_out, B);
  not not_273 (not_273_out, E);
  not not_274 (not_274_out, F);
  not not_275 (not_275_out, D);
  not not_276 (not_276_out, D);
  not not_277 (not_277_out, E);
  not not_278 (not_278_out, C);
  not not_279 (not_279_out, F);
  not not_280 (not_280_out, D);
  not not_281 (not_281_out, F);
  not not_282 (not_282_out, A);
  and and_111 (and_111_out, not_282_out, not_283_out);
  not not_283 (not_283_out, C);
  not not_284 (not_284_out, D);
  not not_285 (not_285_out, E);
  and and_112 (and_112_out, not_285_out, not_286_out);
  not not_286 (not_286_out, F);
  not not_287 (not_287_out, A);
  and and_113 (and_113_out, not_287_out, not_288_out);
  not not_288 (not_288_out, B);
  not not_289 (not_289_out, C);
  not not_290 (not_290_out, E);
  and and_114 (and_114_out, not_290_out, F);
  not not_291 (not_291_out, A);
  not not_292 (not_292_out, C);
  not not_293 (not_293_out, A);
  not not_294 (not_294_out, B);
  not not_295 (not_295_out, C);
  not not_296 (not_296_out, E);
  not not_297 (not_297_out, F);
  not not_298 (not_298_out, A);
  not not_299 (not_299_out, B);
  not not_300 (not_300_out, C);
  not not_301 (not_301_out, F);
  not not_302 (not_302_out, A);
  not not_303 (not_303_out, E);
  not not_304 (not_304_out, F);
  not not_305 (not_305_out, A);
  not not_306 (not_306_out, B);
  not not_307 (not_307_out, E);
  not not_308 (not_308_out, A);
  not not_309 (not_309_out, F);
  not not_310 (not_310_out, A);
  not not_311 (not_311_out, B);
  not not_312 (not_312_out, A);
  not not_313 (not_313_out, B);
  not not_314 (not_314_out, F);
  not not_315 (not_315_out, A);
  not not_316 (not_316_out, D);
  not not_317 (not_317_out, A);
  not not_318 (not_318_out, A);
  not not_319 (not_319_out, E);
  not not_320 (not_320_out, A);
  not not_321 (not_321_out, D);
  not not_322 (not_322_out, E);
  not not_323 (not_323_out, A);
  not not_324 (not_324_out, E);
  not not_325 (not_325_out, A);
  not not_326 (not_326_out, C);
  not not_327 (not_327_out, E);
  and and_115 (and_115_out, A, not_328_out);
  not not_328 (not_328_out, B);
  not not_329 (not_329_out, C);
  and and_116 (and_116_out, E, not_330_out);
  not not_330 (not_330_out, F);
  not not_331 (not_331_out, G);
  and and_117 (and_117_out, A, not_332_out);
  not not_332 (not_332_out, C);
  not not_333 (not_333_out, D);
  and and_118 (and_118_out, E, F);
  not not_334 (not_334_out, B);
  not not_335 (not_335_out, C);
  not not_336 (not_336_out, E);
  not not_337 (not_337_out, F);
  not not_338 (not_338_out, B);
  not not_339 (not_339_out, C);
  not not_340 (not_340_out, F);
  not not_341 (not_341_out, E);
  not not_342 (not_342_out, F);
  not not_343 (not_343_out, B);
  not not_344 (not_344_out, E);
  not not_345 (not_345_out, B);
  not not_346 (not_346_out, E);
  not not_347 (not_347_out, F);
  not not_348 (not_348_out, B);
  not not_349 (not_349_out, F);
  not not_350 (not_350_out, D);
  not not_351 (not_351_out, E);
  not not_352 (not_352_out, E);
  not not_353 (not_353_out, D);
  not not_354 (not_354_out, D);
  not not_355 (not_355_out, E);
  and and_119 (and_119_out, and_1_out, E);
  or or_1 (or_1_out, and_119_out, and_120_out);
  and and_120 (and_120_out, and_2_out, D);
  and and_121 (and_121_out, A, B);
  and and_122 (and_122_out, and_121_out, C);
  and and_123 (and_123_out, and_3_out, and_4_out);
  and and_124 (and_124_out, and_5_out, and_6_out);
  and and_125 (and_125_out, not_3_out, B);
  and and_126 (and_126_out, C, D);
  not not_356 (not_356_out, B);
  and and_127 (and_127_out, A, not_4_out);
  and and_128 (and_128_out, not_5_out, not_6_out);
  and and_129 (and_129_out, not_7_out, B);
  and and_130 (and_130_out, not_8_out, D);
  and and_131 (and_131_out, and_7_out, C);
  and and_132 (and_132_out, and_8_out, not_12_out);
  and and_133 (and_133_out, A, not_13_out);
  and and_134 (and_134_out, A, not_14_out);
  and and_135 (and_135_out, A, B);
  not not_357 (not_357_out, C);
  not not_358 (not_358_out, D);
  not not_359 (not_359_out, E);
  and and_136 (and_136_out, not_15_out, C);
  and and_137 (and_137_out, not_16_out, E);
  and and_138 (and_138_out, not_17_out, not_18_out);
  and and_139 (and_139_out, C, D);
  and and_140 (and_140_out, not_19_out, B);
  and and_141 (and_141_out, not_20_out, not_21_out);
  and and_142 (and_142_out, and_9_out, not_23_out);
  and and_143 (and_143_out, E, F);
  and and_144 (and_144_out, A, not_24_out);
  and and_145 (and_145_out, not_25_out, D);
  and and_146 (and_146_out, A, not_26_out);
  and and_147 (and_147_out, C, not_27_out);
  and and_148 (and_148_out, and_10_out, C);
  and and_149 (and_149_out, not_29_out, not_30_out);
  and and_150 (and_150_out, A, B);
  and and_151 (and_151_out, C, D);
  and and_152 (and_152_out, and_11_out, not_33_out);
  and and_153 (and_153_out, D, F);
  and and_154 (and_154_out, and_12_out, not_36_out);
  and and_155 (and_155_out, D, E);
  and and_156 (and_156_out, not_37_out, not_38_out);
  and and_157 (and_157_out, not_39_out, C);
  and and_158 (and_158_out, not_40_out, not_41_out);
  and and_159 (and_159_out, not_42_out, B);
  and and_160 (and_160_out, not_43_out, not_44_out);
  and and_161 (and_161_out, not_45_out, B);
  and and_162 (and_162_out, A, not_46_out);
  and and_163 (and_163_out, not_47_out, not_48_out);
  and and_164 (and_164_out, A, not_49_out);
  and and_165 (and_165_out, not_50_out, not_51_out);
  and and_166 (and_166_out, A, not_52_out);
  not not_360 (not_360_out, E);
  not not_361 (not_361_out, F);
  and and_167 (and_167_out, A, B);
  not not_362 (not_362_out, C);
  and and_168 (and_168_out, D, E);
  and and_169 (and_169_out, and_13_out, not_55_out);
  and and_170 (and_170_out, E, G);
  and and_171 (and_171_out, and_14_out, not_58_out);
  and and_172 (and_172_out, E, F);
  and and_173 (and_173_out, and_15_out, E);
  and and_174 (and_174_out, F, G);
  and and_175 (and_175_out, and_16_out, not_63_out);
  and and_176 (and_176_out, and_17_out, not_65_out);
  and and_177 (and_177_out, and_18_out, C);
  and and_178 (and_178_out, not_68_out, not_69_out);
  and and_179 (and_179_out, and_19_out, C);
  and and_180 (and_180_out, not_72_out, G);
  and and_181 (and_181_out, and_20_out, D);
  and and_182 (and_182_out, not_74_out, F);
  and and_183 (and_183_out, and_21_out, C);
  and and_184 (and_184_out, and_22_out, not_77_out);
  and and_185 (and_185_out, and_23_out, not_79_out);
  and and_186 (and_186_out, and_24_out, G);
  and and_187 (and_187_out, and_25_out, not_82_out);
  and and_188 (and_188_out, not_83_out, E);
  and and_189 (and_189_out, and_26_out, not_85_out);
  and and_190 (and_190_out, E, G);
  and and_191 (and_191_out, and_27_out, not_87_out);
  and and_192 (and_192_out, E, F);
  and and_193 (and_193_out, and_28_out, not_89_out);
  and and_194 (and_194_out, and_29_out, G);
  and and_195 (and_195_out, and_30_out, C);
  and and_196 (and_196_out, not_91_out, not_92_out);
  and and_197 (and_197_out, and_31_out, not_94_out);
  and and_198 (and_198_out, not_95_out, G);
  and and_199 (and_199_out, and_32_out, not_97_out);
  and and_200 (and_200_out, not_98_out, F);
  and and_201 (and_201_out, and_33_out, not_100_out);
  and and_202 (and_202_out, F, G);
  and and_203 (and_203_out, and_34_out, not_102_out);
  and and_204 (and_204_out, E, not_103_out);
  and and_205 (and_205_out, and_35_out, not_105_out);
  and and_206 (and_206_out, D, E);
  and and_207 (and_207_out, and_36_out, D);
  and and_208 (and_208_out, E, not_107_out);
  and and_209 (and_209_out, and_37_out, not_108_out);
  and and_210 (and_210_out, E, G);
  and and_211 (and_211_out, and_38_out, not_109_out);
  and and_212 (and_212_out, E, F);
  and and_213 (and_213_out, and_39_out, E);
  and and_214 (and_214_out, F, G);
  and and_215 (and_215_out, and_40_out, C);
  and and_216 (and_216_out, and_41_out, not_112_out);
  and and_217 (and_217_out, and_42_out, not_113_out);
  and and_218 (and_218_out, not_114_out, not_115_out);
  and and_219 (and_219_out, and_43_out, not_116_out);
  and and_220 (and_220_out, not_117_out, G);
  and and_221 (and_221_out, and_44_out, not_118_out);
  and and_222 (and_222_out, not_119_out, F);
  and and_223 (and_223_out, and_45_out, not_120_out);
  and and_224 (and_224_out, and_46_out, G);
  and and_225 (and_225_out, and_47_out, C);
  and and_226 (and_226_out, not_122_out, E);
  and and_227 (and_227_out, and_48_out, C);
  and and_228 (and_228_out, E, G);
  and and_229 (and_229_out, A, B);
  and and_230 (and_230_out, and_49_out, and_50_out);
  and and_231 (and_231_out, and_51_out, not_128_out);
  and and_232 (and_232_out, and_52_out, and_53_out);
  and and_233 (and_233_out, and_54_out, G);
  and and_234 (and_234_out, and_55_out, and_56_out);
  and and_235 (and_235_out, and_57_out, not_137_out);
  and and_236 (and_236_out, and_58_out, and_59_out);
  and and_237 (and_237_out, and_60_out, G);
  and and_238 (and_238_out, and_61_out, and_62_out);
  and and_239 (and_239_out, and_63_out, not_146_out);
  and and_240 (and_240_out, and_64_out, and_65_out);
  and and_241 (and_241_out, and_66_out, G);
  and and_242 (and_242_out, not_150_out, B);
  and and_243 (and_243_out, not_151_out, not_152_out);
  and and_244 (and_244_out, not_153_out, F);
  not not_363 (not_363_out, G);
  and and_245 (and_245_out, and_67_out, and_68_out);
  and and_246 (and_246_out, and_69_out, G);
  and and_247 (and_247_out, and_70_out, and_71_out);
  and and_248 (and_248_out, and_72_out, not_160_out);
  and and_249 (and_249_out, not_161_out, B);
  and and_250 (and_250_out, C, not_162_out);
  and and_251 (and_251_out, not_163_out, not_164_out);
  and and_252 (and_252_out, and_73_out, and_74_out);
  and and_253 (and_253_out, and_75_out, not_167_out);
  and and_254 (and_254_out, and_76_out, and_77_out);
  and and_255 (and_255_out, and_78_out, G);
  and and_256 (and_256_out, A, not_170_out);
  and and_257 (and_257_out, not_171_out, not_172_out);
  and and_258 (and_258_out, not_173_out, not_174_out);
  not not_364 (not_364_out, G);
  and and_259 (and_259_out, and_79_out, and_80_out);
  and and_260 (and_260_out, and_81_out, G);
  and and_261 (and_261_out, and_82_out, and_83_out);
  and and_262 (and_262_out, and_84_out, not_182_out);
  and and_263 (and_263_out, A, not_183_out);
  and and_264 (and_264_out, not_184_out, D);
  and and_265 (and_265_out, E, F);
  and and_266 (and_266_out, and_85_out, and_86_out);
  and and_267 (and_267_out, and_87_out, not_188_out);
  and and_268 (and_268_out, and_88_out, and_89_out);
  and and_269 (and_269_out, and_90_out, G);
  and and_270 (and_270_out, A, not_192_out);
  and and_271 (and_271_out, C, D);
  and and_272 (and_272_out, E, F);
  not not_365 (not_365_out, G);
  and and_273 (and_273_out, and_91_out, and_92_out);
  and and_274 (and_274_out, and_93_out, G);
  and and_275 (and_275_out, and_94_out, and_95_out);
  and and_276 (and_276_out, and_96_out, not_199_out);
  and and_277 (and_277_out, A, B);
  and and_278 (and_278_out, not_200_out, D);
  and and_279 (and_279_out, E, not_201_out);
  and and_280 (and_280_out, and_97_out, and_98_out);
  and and_281 (and_281_out, and_99_out, not_204_out);
  and and_282 (and_282_out, and_100_out, and_101_out);
  and and_283 (and_283_out, and_102_out, G);
  and and_284 (and_284_out, A, B);
  and and_285 (and_285_out, C, D);
  and and_286 (and_286_out, E, not_206_out);
  not not_366 (not_366_out, G);
  and and_287 (and_287_out, and_103_out, not_209_out);
  and and_288 (and_288_out, and_104_out, F);
  and and_289 (and_289_out, and_105_out, not_214_out);
  and and_290 (and_290_out, and_106_out, G);
  and and_291 (and_291_out, not_216_out, not_217_out);
  and and_292 (and_292_out, not_218_out, not_219_out);
  not not_367 (not_367_out, G);
  and and_293 (and_293_out, not_220_out, not_221_out);
  not not_368 (not_368_out, C);
  and and_294 (and_294_out, D, E);
  not not_369 (not_369_out, F);
  and and_295 (and_295_out, not_222_out, not_223_out);
  and and_296 (and_296_out, E, not_224_out);
  not not_370 (not_370_out, G);
  and and_297 (and_297_out, not_225_out, not_226_out);
  and and_298 (and_298_out, C, not_227_out);
  and and_299 (and_299_out, not_228_out, not_229_out);
  and and_300 (and_300_out, not_230_out, C);
  not not_371 (not_371_out, D);
  and and_301 (and_301_out, not_231_out, F);
  not not_372 (not_372_out, G);
  and and_302 (and_302_out, not_232_out, not_233_out);
  and and_303 (and_303_out, not_234_out, E);
  and and_304 (and_304_out, not_235_out, not_236_out);
  and and_305 (and_305_out, C, D);
  and and_306 (and_306_out, not_237_out, F);
  and and_307 (and_307_out, not_238_out, B);
  not not_373 (not_373_out, C);
  and and_308 (and_308_out, not_239_out, not_240_out);
  not not_374 (not_374_out, F);
  and and_309 (and_309_out, not_241_out, B);
  not not_375 (not_375_out, C);
  and and_310 (and_310_out, not_242_out, not_243_out);
  and and_311 (and_311_out, B, not_244_out);
  not not_376 (not_376_out, D);
  and and_312 (and_312_out, E, F);
  not not_377 (not_377_out, G);
  and and_313 (and_313_out, not_245_out, B);
  not not_378 (not_378_out, C);
  and and_314 (and_314_out, D, not_246_out);
  and and_315 (and_315_out, not_247_out, B);
  not not_379 (not_379_out, C);
  and and_316 (and_316_out, D, F);
  and and_317 (and_317_out, B, C);
  not not_380 (not_380_out, D);
  and and_318 (and_318_out, not_248_out, not_249_out);
  not not_381 (not_381_out, G);
  and and_319 (and_319_out, not_250_out, B);
  and and_320 (and_320_out, not_251_out, E);
  not not_382 (not_382_out, F);
  and and_321 (and_321_out, not_252_out, B);
  and and_322 (and_322_out, C, D);
  and and_323 (and_323_out, not_253_out, not_254_out);
  and and_324 (and_324_out, and_107_out, D);
  and and_325 (and_325_out, and_108_out, not_256_out);
  and and_326 (and_326_out, and_109_out, C);
  and and_327 (and_327_out, and_110_out, F);
  and and_328 (and_328_out, A, not_258_out);
  not not_383 (not_383_out, D);
  and and_329 (and_329_out, not_259_out, F);
  and and_330 (and_330_out, A, not_260_out);
  and and_331 (and_331_out, not_261_out, not_262_out);
  and and_332 (and_332_out, E, not_263_out);
  not not_384 (not_384_out, G);
  and and_333 (and_333_out, A, not_264_out);
  not not_385 (not_385_out, C);
  and and_334 (and_334_out, D, not_265_out);
  and and_335 (and_335_out, A, not_266_out);
  and and_336 (and_336_out, not_267_out, D);
  and and_337 (and_337_out, E, F);
  not not_386 (not_386_out, G);
  and and_338 (and_338_out, A, not_268_out);
  and and_339 (and_339_out, not_269_out, F);
  and and_340 (and_340_out, A, not_270_out);
  and and_341 (and_341_out, D, not_271_out);
  not not_387 (not_387_out, G);
  and and_342 (and_342_out, A, not_272_out);
  and and_343 (and_343_out, D, E);
  not not_388 (not_388_out, F);
  and and_344 (and_344_out, A, B);
  not not_389 (not_389_out, D);
  and and_345 (and_345_out, not_273_out, not_274_out);
  and and_346 (and_346_out, A, B);
  not not_390 (not_390_out, C);
  and and_347 (and_347_out, not_275_out, F);
  not not_391 (not_391_out, G);
  and and_348 (and_348_out, A, B);
  not not_392 (not_392_out, C);
  and and_349 (and_349_out, not_276_out, E);
  and and_350 (and_350_out, A, B);
  not not_393 (not_393_out, D);
  and and_351 (and_351_out, E, F);
  not not_394 (not_394_out, G);
  and and_352 (and_352_out, A, B);
  and and_353 (and_353_out, not_277_out, F);
  and and_354 (and_354_out, A, B);
  and and_355 (and_355_out, not_278_out, D);
  and and_356 (and_356_out, E, not_279_out);
  not not_395 (not_395_out, G);
  and and_357 (and_357_out, A, B);
  and and_358 (and_358_out, not_280_out, not_281_out);
  and and_359 (and_359_out, A, B);
  and and_360 (and_360_out, D, F);
  and and_361 (and_361_out, and_111_out, not_284_out);
  and and_362 (and_362_out, and_112_out, G);
  and and_363 (and_363_out, and_113_out, not_289_out);
  and and_364 (and_364_out, and_114_out, G);
  and and_365 (and_365_out, not_291_out, not_292_out);
  not not_396 (not_396_out, D);
  and and_366 (and_366_out, E, F);
  not not_397 (not_397_out, G);
  and and_367 (and_367_out, not_293_out, not_294_out);
  and and_368 (and_368_out, not_295_out, D);
  and and_369 (and_369_out, not_296_out, not_297_out);
  not not_398 (not_398_out, G);
  and and_370 (and_370_out, not_298_out, not_299_out);
  and and_371 (and_371_out, not_300_out, D);
  and and_372 (and_372_out, E, not_301_out);
  and and_373 (and_373_out, not_302_out, C);
  not not_399 (not_399_out, D);
  and and_374 (and_374_out, not_303_out, not_304_out);
  not not_400 (not_400_out, G);
  and and_375 (and_375_out, not_305_out, not_306_out);
  and and_376 (and_376_out, not_307_out, F);
  not not_401 (not_401_out, G);
  and and_377 (and_377_out, not_308_out, C);
  not not_402 (not_402_out, D);
  and and_378 (and_378_out, E, not_309_out);
  and and_379 (and_379_out, not_310_out, not_311_out);
  and and_380 (and_380_out, E, F);
  and and_381 (and_381_out, not_312_out, not_313_out);
  and and_382 (and_382_out, C, D);
  and and_383 (and_383_out, E, not_314_out);
  not not_403 (not_403_out, G);
  and and_384 (and_384_out, not_315_out, B);
  not not_404 (not_404_out, C);
  and and_385 (and_385_out, not_316_out, E);
  not not_405 (not_405_out, G);
  and and_386 (and_386_out, not_317_out, B);
  not not_406 (not_406_out, C);
  and and_387 (and_387_out, E, F);
  not not_407 (not_407_out, G);
  and and_388 (and_388_out, not_318_out, B);
  not not_408 (not_408_out, C);
  and and_389 (and_389_out, D, not_319_out);
  and and_390 (and_390_out, not_320_out, B);
  and and_391 (and_391_out, C, not_321_out);
  and and_392 (and_392_out, not_322_out, F);
  and and_393 (and_393_out, not_323_out, B);
  and and_394 (and_394_out, D, not_324_out);
  not not_409 (not_409_out, G);
  and and_395 (and_395_out, not_325_out, B);
  and and_396 (and_396_out, D, E);
  and and_397 (and_397_out, A, not_326_out);
  not not_410 (not_410_out, D);
  and and_398 (and_398_out, not_327_out, F);
  not not_411 (not_411_out, G);
  and and_399 (and_399_out, and_115_out, not_329_out);
  and and_400 (and_400_out, and_116_out, not_331_out);
  and and_401 (and_401_out, and_117_out, not_333_out);
  and and_402 (and_402_out, and_118_out, G);
  and and_403 (and_403_out, A, not_334_out);
  and and_404 (and_404_out, not_335_out, D);
  and and_405 (and_405_out, not_336_out, not_337_out);
  and and_406 (and_406_out, A, not_338_out);
  not not_412 (not_412_out, C);
  and and_407 (and_407_out, D, E);
  not not_413 (not_413_out, G);
  and and_408 (and_408_out, A, not_339_out);
  and and_409 (and_409_out, E, not_340_out);
  not not_414 (not_414_out, G);
  and and_410 (and_410_out, A, C);
  not not_415 (not_415_out, D);
  and and_411 (and_411_out, not_341_out, not_342_out);
  and and_412 (and_412_out, A, not_343_out);
  and and_413 (and_413_out, not_344_out, F);
  and and_414 (and_414_out, A, C);
  not not_416 (not_416_out, D);
  and and_415 (and_415_out, E, F);
  not not_417 (not_417_out, G);
  and and_416 (and_416_out, A, not_345_out);
  and and_417 (and_417_out, C, D);
  and and_418 (and_418_out, not_346_out, not_347_out);
  not not_418 (not_418_out, G);
  and and_419 (and_419_out, A, not_348_out);
  and and_420 (and_420_out, C, D);
  and and_421 (and_421_out, E, not_349_out);
  and and_422 (and_422_out, A, B);
  not not_419 (not_419_out, C);
  and and_423 (and_423_out, not_350_out, not_351_out);
  not not_420 (not_420_out, G);
  and and_424 (and_424_out, A, B);
  not not_421 (not_421_out, C);
  and and_425 (and_425_out, not_352_out, F);
  not not_422 (not_422_out, G);
  and and_426 (and_426_out, A, B);
  not not_423 (not_423_out, C);
  and and_427 (and_427_out, not_353_out, E);
  and and_428 (and_428_out, A, B);
  not not_424 (not_424_out, C);
  and and_429 (and_429_out, E, F);
  and and_430 (and_430_out, A, B);
  and and_431 (and_431_out, not_354_out, E);
  not not_425 (not_425_out, G);
  and and_432 (and_432_out, A, B);
  and and_433 (and_433_out, E, F);
  not not_426 (not_426_out, G);
  and and_434 (and_434_out, A, B);
  and and_435 (and_435_out, D, not_355_out);
  or or_2 (H1, or_1_out, and_122_out);
  or or_3 (or_3_out, and_123_out, and_124_out);
  and and_436 (and_436_out, and_125_out, and_126_out);
  and and_437 (and_437_out, A, not_356_out);
  and and_438 (and_438_out, and_127_out, and_128_out);
  and and_439 (and_439_out, and_129_out, and_130_out);
  and and_440 (and_440_out, and_131_out, and_132_out);
  and and_441 (and_441_out, and_133_out, C);
  and and_442 (and_442_out, D, F);
  and and_443 (and_443_out, and_134_out, C);
  and and_444 (and_444_out, D, E);
  and and_445 (and_445_out, and_135_out, not_357_out);
  and and_446 (and_446_out, not_358_out, not_359_out);
  and and_447 (and_447_out, and_136_out, and_137_out);
  and and_448 (and_448_out, and_138_out, and_139_out);
  and and_449 (and_449_out, and_140_out, and_141_out);
  and and_450 (and_450_out, and_142_out, and_143_out);
  and and_451 (and_451_out, and_144_out, and_145_out);
  and and_452 (and_452_out, and_146_out, and_147_out);
  and and_453 (and_453_out, and_148_out, and_149_out);
  and and_454 (and_454_out, and_150_out, and_151_out);
  and and_455 (and_455_out, and_152_out, and_153_out);
  and and_456 (and_456_out, and_154_out, and_155_out);
  and and_457 (and_457_out, and_156_out, D);
  and and_458 (and_458_out, E, F);
  and and_459 (and_459_out, and_157_out, and_158_out);
  and and_460 (and_460_out, and_159_out, and_160_out);
  and and_461 (and_461_out, and_161_out, C);
  and and_462 (and_462_out, D, E);
  and and_463 (and_463_out, and_162_out, and_163_out);
  and and_464 (and_464_out, and_164_out, and_165_out);
  and and_465 (and_465_out, and_166_out, C);
  and and_466 (and_466_out, not_360_out, not_361_out);
  and and_467 (and_467_out, A, C);
  not not_427 (not_427_out, D);
  and and_468 (and_468_out, and_167_out, not_362_out);
  and and_469 (and_469_out, and_168_out, F);
  and and_470 (and_470_out, and_169_out, and_170_out);
  and and_471 (and_471_out, and_171_out, and_172_out);
  and and_472 (and_472_out, and_173_out, and_174_out);
  and and_473 (and_473_out, and_175_out, and_176_out);
  and and_474 (and_474_out, and_177_out, and_178_out);
  and and_475 (and_475_out, and_179_out, and_180_out);
  and and_476 (and_476_out, and_181_out, and_182_out);
  and and_477 (and_477_out, and_183_out, and_184_out);
  and and_478 (and_478_out, and_185_out, and_186_out);
  and and_479 (and_479_out, and_187_out, and_188_out);
  and and_480 (and_480_out, and_189_out, and_190_out);
  and and_481 (and_481_out, and_191_out, and_192_out);
  and and_482 (and_482_out, and_193_out, and_194_out);
  and and_483 (and_483_out, and_195_out, and_196_out);
  and and_484 (and_484_out, and_197_out, and_198_out);
  and and_485 (and_485_out, and_199_out, and_200_out);
  and and_486 (and_486_out, and_201_out, and_202_out);
  and and_487 (and_487_out, and_203_out, and_204_out);
  and and_488 (and_488_out, and_205_out, and_206_out);
  and and_489 (and_489_out, and_207_out, and_208_out);
  and and_490 (and_490_out, and_209_out, and_210_out);
  and and_491 (and_491_out, and_211_out, and_212_out);
  and and_492 (and_492_out, and_213_out, and_214_out);
  and and_493 (and_493_out, and_215_out, and_216_out);
  and and_494 (and_494_out, and_217_out, and_218_out);
  and and_495 (and_495_out, and_219_out, and_220_out);
  and and_496 (and_496_out, and_221_out, and_222_out);
  and and_497 (and_497_out, and_223_out, and_224_out);
  and and_498 (and_498_out, and_225_out, and_226_out);
  and and_499 (and_499_out, and_227_out, and_228_out);
  and and_500 (and_500_out, and_229_out, C);
  and and_501 (and_501_out, E, F);
  and and_502 (and_502_out, and_230_out, and_231_out);
  and and_503 (and_503_out, and_232_out, and_233_out);
  and and_504 (and_504_out, and_234_out, and_235_out);
  and and_505 (and_505_out, and_236_out, and_237_out);
  and and_506 (and_506_out, and_238_out, and_239_out);
  and and_507 (and_507_out, and_240_out, and_241_out);
  and and_508 (and_508_out, and_242_out, and_243_out);
  and and_509 (and_509_out, and_244_out, not_363_out);
  and and_510 (and_510_out, and_245_out, and_246_out);
  and and_511 (and_511_out, and_247_out, and_248_out);
  and and_512 (and_512_out, and_249_out, and_250_out);
  and and_513 (and_513_out, and_251_out, G);
  and and_514 (and_514_out, and_252_out, and_253_out);
  and and_515 (and_515_out, and_254_out, and_255_out);
  and and_516 (and_516_out, and_256_out, and_257_out);
  and and_517 (and_517_out, and_258_out, not_364_out);
  and and_518 (and_518_out, and_259_out, and_260_out);
  and and_519 (and_519_out, and_261_out, and_262_out);
  and and_520 (and_520_out, and_263_out, and_264_out);
  and and_521 (and_521_out, and_265_out, G);
  and and_522 (and_522_out, and_266_out, and_267_out);
  and and_523 (and_523_out, and_268_out, and_269_out);
  and and_524 (and_524_out, and_270_out, and_271_out);
  and and_525 (and_525_out, and_272_out, not_365_out);
  and and_526 (and_526_out, and_273_out, and_274_out);
  and and_527 (and_527_out, and_275_out, and_276_out);
  and and_528 (and_528_out, and_277_out, and_278_out);
  and and_529 (and_529_out, and_279_out, G);
  and and_530 (and_530_out, and_280_out, and_281_out);
  and and_531 (and_531_out, and_282_out, and_283_out);
  and and_532 (and_532_out, and_284_out, and_285_out);
  and and_533 (and_533_out, and_286_out, not_366_out);
  and and_534 (and_534_out, and_287_out, and_288_out);
  and and_535 (and_535_out, and_289_out, and_290_out);
  and and_536 (and_536_out, and_291_out, D);
  and and_537 (and_537_out, and_292_out, not_367_out);
  and and_538 (and_538_out, and_293_out, not_368_out);
  and and_539 (and_539_out, and_294_out, not_369_out);
  and and_540 (and_540_out, and_295_out, D);
  and and_541 (and_541_out, and_296_out, not_370_out);
  and and_542 (and_542_out, and_297_out, and_298_out);
  and and_543 (and_543_out, and_299_out, G);
  and and_544 (and_544_out, and_300_out, not_371_out);
  and and_545 (and_545_out, and_301_out, not_372_out);
  and and_546 (and_546_out, and_302_out, C);
  and and_547 (and_547_out, and_303_out, F);
  and and_548 (and_548_out, and_304_out, and_305_out);
  and and_549 (and_549_out, and_306_out, G);
  and and_550 (and_550_out, and_307_out, not_373_out);
  and and_551 (and_551_out, and_308_out, not_374_out);
  and and_552 (and_552_out, and_309_out, not_375_out);
  and and_553 (and_553_out, and_310_out, G);
  and and_554 (and_554_out, and_311_out, not_376_out);
  and and_555 (and_555_out, and_312_out, not_377_out);
  and and_556 (and_556_out, and_313_out, not_378_out);
  and and_557 (and_557_out, and_314_out, F);
  and and_558 (and_558_out, and_315_out, not_379_out);
  and and_559 (and_559_out, and_316_out, G);
  and and_560 (and_560_out, and_317_out, not_380_out);
  and and_561 (and_561_out, and_318_out, not_381_out);
  and and_562 (and_562_out, and_319_out, C);
  and and_563 (and_563_out, and_320_out, not_382_out);
  and and_564 (and_564_out, and_321_out, and_322_out);
  and and_565 (and_565_out, and_323_out, G);
  and and_566 (and_566_out, and_324_out, and_325_out);
  and and_567 (and_567_out, and_326_out, and_327_out);
  and and_568 (and_568_out, and_328_out, not_383_out);
  and and_569 (and_569_out, and_329_out, G);
  and and_570 (and_570_out, and_330_out, and_331_out);
  and and_571 (and_571_out, and_332_out, not_384_out);
  and and_572 (and_572_out, and_333_out, not_385_out);
  and and_573 (and_573_out, and_334_out, G);
  and and_574 (and_574_out, and_335_out, and_336_out);
  and and_575 (and_575_out, and_337_out, not_386_out);
  and and_576 (and_576_out, and_338_out, C);
  and and_577 (and_577_out, and_339_out, G);
  and and_578 (and_578_out, and_340_out, C);
  and and_579 (and_579_out, and_341_out, not_387_out);
  and and_580 (and_580_out, and_342_out, C);
  and and_581 (and_581_out, and_343_out, not_388_out);
  and and_582 (and_582_out, and_344_out, not_389_out);
  and and_583 (and_583_out, and_345_out, G);
  and and_584 (and_584_out, and_346_out, not_390_out);
  and and_585 (and_585_out, and_347_out, not_391_out);
  and and_586 (and_586_out, and_348_out, not_392_out);
  and and_587 (and_587_out, and_349_out, F);
  and and_588 (and_588_out, and_350_out, not_393_out);
  and and_589 (and_589_out, and_351_out, not_394_out);
  and and_590 (and_590_out, and_352_out, D);
  and and_591 (and_591_out, and_353_out, G);
  and and_592 (and_592_out, and_354_out, and_355_out);
  and and_593 (and_593_out, and_356_out, not_395_out);
  and and_594 (and_594_out, and_357_out, C);
  and and_595 (and_595_out, and_358_out, G);
  and and_596 (and_596_out, and_359_out, C);
  and and_597 (and_597_out, and_360_out, G);
  and and_598 (and_598_out, and_361_out, and_362_out);
  and and_599 (and_599_out, and_363_out, and_364_out);
  and and_600 (and_600_out, and_365_out, not_396_out);
  and and_601 (and_601_out, and_366_out, not_397_out);
  and and_602 (and_602_out, and_367_out, and_368_out);
  and and_603 (and_603_out, and_369_out, not_398_out);
  and and_604 (and_604_out, and_370_out, and_371_out);
  and and_605 (and_605_out, and_372_out, G);
  and and_606 (and_606_out, and_373_out, not_399_out);
  and and_607 (and_607_out, and_374_out, not_400_out);
  and and_608 (and_608_out, and_375_out, C);
  and and_609 (and_609_out, and_376_out, not_401_out);
  and and_610 (and_610_out, and_377_out, not_402_out);
  and and_611 (and_611_out, and_378_out, G);
  and and_612 (and_612_out, and_379_out, C);
  and and_613 (and_613_out, and_380_out, G);
  and and_614 (and_614_out, and_381_out, and_382_out);
  and and_615 (and_615_out, and_383_out, not_403_out);
  and and_616 (and_616_out, and_384_out, not_404_out);
  and and_617 (and_617_out, and_385_out, not_405_out);
  and and_618 (and_618_out, and_386_out, not_406_out);
  and and_619 (and_619_out, and_387_out, not_407_out);
  and and_620 (and_620_out, and_388_out, not_408_out);
  and and_621 (and_621_out, and_389_out, G);
  and and_622 (and_622_out, and_390_out, and_391_out);
  and and_623 (and_623_out, and_392_out, G);
  and and_624 (and_624_out, and_393_out, C);
  and and_625 (and_625_out, and_394_out, not_409_out);
  and and_626 (and_626_out, and_395_out, C);
  and and_627 (and_627_out, and_396_out, G);
  and and_628 (and_628_out, and_397_out, not_410_out);
  and and_629 (and_629_out, and_398_out, not_411_out);
  and and_630 (and_630_out, and_399_out, and_400_out);
  and and_631 (and_631_out, and_401_out, and_402_out);
  and and_632 (and_632_out, and_403_out, and_404_out);
  and and_633 (and_633_out, and_405_out, G);
  and and_634 (and_634_out, and_406_out, not_412_out);
  and and_635 (and_635_out, and_407_out, not_413_out);
  and and_636 (and_636_out, and_408_out, D);
  and and_637 (and_637_out, and_409_out, not_414_out);
  and and_638 (and_638_out, and_410_out, not_415_out);
  and and_639 (and_639_out, and_411_out, G);
  and and_640 (and_640_out, and_412_out, C);
  and and_641 (and_641_out, and_413_out, G);
  and and_642 (and_642_out, and_414_out, not_416_out);
  and and_643 (and_643_out, and_415_out, not_417_out);
  and and_644 (and_644_out, and_416_out, and_417_out);
  and and_645 (and_645_out, and_418_out, not_418_out);
  and and_646 (and_646_out, and_419_out, and_420_out);
  and and_647 (and_647_out, and_421_out, G);
  and and_648 (and_648_out, and_422_out, not_419_out);
  and and_649 (and_649_out, and_423_out, not_420_out);
  and and_650 (and_650_out, and_424_out, not_421_out);
  and and_651 (and_651_out, and_425_out, not_422_out);
  and and_652 (and_652_out, and_426_out, not_423_out);
  and and_653 (and_653_out, and_427_out, G);
  and and_654 (and_654_out, and_428_out, not_424_out);
  and and_655 (and_655_out, and_429_out, G);
  and and_656 (and_656_out, and_430_out, C);
  and and_657 (and_657_out, and_431_out, not_425_out);
  and and_658 (and_658_out, and_432_out, C);
  and and_659 (and_659_out, and_433_out, not_426_out);
  and and_660 (and_660_out, and_434_out, C);
  and and_661 (and_661_out, and_435_out, G);
  or or_4 (or_4_out, or_3_out, and_436_out);
  or or_5 (or_5_out, and_437_out, and_438_out);
  or or_6 (or_6_out, and_439_out, and_440_out);
  and and_662 (and_662_out, and_441_out, and_442_out);
  and and_663 (and_663_out, and_443_out, and_444_out);
  and and_664 (and_664_out, and_445_out, and_446_out);
  or or_7 (or_7_out, and_447_out, and_448_out);
  or or_8 (or_8_out, and_449_out, and_450_out);
  or or_9 (or_9_out, and_451_out, and_452_out);
  or or_10 (or_10_out, and_453_out, and_454_out);
  or or_11 (or_11_out, and_455_out, and_456_out);
  and and_665 (and_665_out, and_457_out, and_458_out);
  or or_12 (or_12_out, and_459_out, and_460_out);
  and and_666 (and_666_out, and_461_out, and_462_out);
  or or_13 (or_13_out, and_463_out, and_464_out);
  and and_667 (and_667_out, and_465_out, and_466_out);
  and and_668 (and_668_out, and_467_out, not_427_out);
  and and_669 (and_669_out, and_468_out, and_469_out);
  or or_14 (or_14_out, and_470_out, and_471_out);
  or or_15 (or_15_out, and_472_out, and_473_out);
  or or_16 (or_16_out, and_474_out, and_475_out);
  or or_17 (or_17_out, and_476_out, and_477_out);
  or or_18 (or_18_out, and_478_out, and_479_out);
  or or_19 (or_19_out, and_480_out, and_481_out);
  or or_20 (or_20_out, and_482_out, and_483_out);
  or or_21 (or_21_out, and_484_out, and_485_out);
  or or_22 (or_22_out, and_486_out, and_487_out);
  or or_23 (or_23_out, and_488_out, and_489_out);
  or or_24 (or_24_out, and_490_out, and_491_out);
  or or_25 (or_25_out, and_492_out, and_493_out);
  or or_26 (or_26_out, and_494_out, and_495_out);
  or or_27 (or_27_out, and_496_out, and_497_out);
  or or_28 (or_28_out, and_498_out, and_499_out);
  and and_670 (and_670_out, and_500_out, and_501_out);
  or or_29 (or_29_out, and_502_out, and_503_out);
  or or_30 (or_30_out, and_504_out, and_505_out);
  or or_31 (or_31_out, and_506_out, and_507_out);
  and and_671 (and_671_out, and_508_out, and_509_out);
  or or_32 (or_32_out, and_510_out, and_511_out);
  and and_672 (and_672_out, and_512_out, and_513_out);
  or or_33 (or_33_out, and_514_out, and_515_out);
  and and_673 (and_673_out, and_516_out, and_517_out);
  or or_34 (or_34_out, and_518_out, and_519_out);
  and and_674 (and_674_out, and_520_out, and_521_out);
  or or_35 (or_35_out, and_522_out, and_523_out);
  and and_675 (and_675_out, and_524_out, and_525_out);
  or or_36 (or_36_out, and_526_out, and_527_out);
  and and_676 (and_676_out, and_528_out, and_529_out);
  or or_37 (or_37_out, and_530_out, and_531_out);
  and and_677 (and_677_out, and_532_out, and_533_out);
  or or_38 (or_38_out, and_534_out, and_535_out);
  and and_678 (and_678_out, and_536_out, and_537_out);
  and and_679 (and_679_out, and_538_out, and_539_out);
  and and_680 (and_680_out, and_540_out, and_541_out);
  and and_681 (and_681_out, and_542_out, and_543_out);
  and and_682 (and_682_out, and_544_out, and_545_out);
  and and_683 (and_683_out, and_546_out, and_547_out);
  and and_684 (and_684_out, and_548_out, and_549_out);
  and and_685 (and_685_out, and_550_out, and_551_out);
  and and_686 (and_686_out, and_552_out, and_553_out);
  and and_687 (and_687_out, and_554_out, and_555_out);
  and and_688 (and_688_out, and_556_out, and_557_out);
  and and_689 (and_689_out, and_558_out, and_559_out);
  and and_690 (and_690_out, and_560_out, and_561_out);
  and and_691 (and_691_out, and_562_out, and_563_out);
  and and_692 (and_692_out, and_564_out, and_565_out);
  or or_39 (or_39_out, and_566_out, and_567_out);
  and and_693 (and_693_out, and_568_out, and_569_out);
  and and_694 (and_694_out, and_570_out, and_571_out);
  and and_695 (and_695_out, and_572_out, and_573_out);
  and and_696 (and_696_out, and_574_out, and_575_out);
  and and_697 (and_697_out, and_576_out, and_577_out);
  and and_698 (and_698_out, and_578_out, and_579_out);
  and and_699 (and_699_out, and_580_out, and_581_out);
  and and_700 (and_700_out, and_582_out, and_583_out);
  and and_701 (and_701_out, and_584_out, and_585_out);
  and and_702 (and_702_out, and_586_out, and_587_out);
  and and_703 (and_703_out, and_588_out, and_589_out);
  and and_704 (and_704_out, and_590_out, and_591_out);
  and and_705 (and_705_out, and_592_out, and_593_out);
  and and_706 (and_706_out, and_594_out, and_595_out);
  and and_707 (and_707_out, and_596_out, and_597_out);
  or or_40 (or_40_out, and_598_out, and_599_out);
  and and_708 (and_708_out, and_600_out, and_601_out);
  and and_709 (and_709_out, and_602_out, and_603_out);
  and and_710 (and_710_out, and_604_out, and_605_out);
  and and_711 (and_711_out, and_606_out, and_607_out);
  and and_712 (and_712_out, and_608_out, and_609_out);
  and and_713 (and_713_out, and_610_out, and_611_out);
  and and_714 (and_714_out, and_612_out, and_613_out);
  and and_715 (and_715_out, and_614_out, and_615_out);
  and and_716 (and_716_out, and_616_out, and_617_out);
  and and_717 (and_717_out, and_618_out, and_619_out);
  and and_718 (and_718_out, and_620_out, and_621_out);
  and and_719 (and_719_out, and_622_out, and_623_out);
  and and_720 (and_720_out, and_624_out, and_625_out);
  and and_721 (and_721_out, and_626_out, and_627_out);
  and and_722 (and_722_out, and_628_out, and_629_out);
  or or_41 (or_41_out, and_630_out, and_631_out);
  and and_723 (and_723_out, and_632_out, and_633_out);
  and and_724 (and_724_out, and_634_out, and_635_out);
  and and_725 (and_725_out, and_636_out, and_637_out);
  and and_726 (and_726_out, and_638_out, and_639_out);
  and and_727 (and_727_out, and_640_out, and_641_out);
  and and_728 (and_728_out, and_642_out, and_643_out);
  and and_729 (and_729_out, and_644_out, and_645_out);
  and and_730 (and_730_out, and_646_out, and_647_out);
  and and_731 (and_731_out, and_648_out, and_649_out);
  and and_732 (and_732_out, and_650_out, and_651_out);
  and and_733 (and_733_out, and_652_out, and_653_out);
  and and_734 (and_734_out, and_654_out, and_655_out);
  and and_735 (and_735_out, and_656_out, and_657_out);
  and and_736 (and_736_out, and_658_out, and_659_out);
  and and_737 (and_737_out, and_660_out, and_661_out);
  or or_42 (H0, or_4_out, or_5_out);
  or or_43 (or_43_out, or_6_out, and_662_out);
  or or_44 (or_44_out, and_663_out, and_664_out);
  or or_45 (or_45_out, or_7_out, or_8_out);
  or or_46 (or_46_out, or_9_out, or_10_out);
  or or_47 (or_47_out, or_11_out, and_665_out);
  or or_48 (or_48_out, or_12_out, and_666_out);
  or or_49 (or_49_out, or_13_out, and_667_out);
  or or_50 (or_50_out, and_668_out, and_669_out);
  or or_51 (or_51_out, or_14_out, or_15_out);
  or or_52 (or_52_out, or_16_out, or_17_out);
  or or_53 (or_53_out, or_18_out, or_19_out);
  or or_54 (or_54_out, or_20_out, or_21_out);
  or or_55 (or_55_out, or_22_out, or_23_out);
  or or_56 (or_56_out, or_24_out, or_25_out);
  or or_57 (or_57_out, or_26_out, or_27_out);
  or or_58 (or_58_out, or_28_out, and_670_out);
  or or_59 (or_59_out, or_29_out, or_30_out);
  or or_60 (or_60_out, or_31_out, and_671_out);
  or or_61 (or_61_out, or_32_out, and_672_out);
  or or_62 (or_62_out, or_33_out, and_673_out);
  or or_63 (or_63_out, or_34_out, and_674_out);
  or or_64 (or_64_out, or_35_out, and_675_out);
  or or_65 (or_65_out, or_36_out, and_676_out);
  or or_66 (or_66_out, or_37_out, and_677_out);
  or or_67 (or_67_out, or_38_out, and_678_out);
  or or_68 (or_68_out, and_679_out, and_680_out);
  or or_69 (or_69_out, and_681_out, and_682_out);
  or or_70 (or_70_out, and_683_out, and_684_out);
  or or_71 (or_71_out, and_685_out, and_686_out);
  or or_72 (or_72_out, and_687_out, and_688_out);
  or or_73 (or_73_out, and_689_out, and_690_out);
  or or_74 (or_74_out, and_691_out, and_692_out);
  or or_75 (or_75_out, or_39_out, and_693_out);
  or or_76 (or_76_out, and_694_out, and_695_out);
  or or_77 (or_77_out, and_696_out, and_697_out);
  or or_78 (or_78_out, and_698_out, and_699_out);
  or or_79 (or_79_out, and_700_out, and_701_out);
  or or_80 (or_80_out, and_702_out, and_703_out);
  or or_81 (or_81_out, and_704_out, and_705_out);
  or or_82 (or_82_out, and_706_out, and_707_out);
  or or_83 (or_83_out, or_40_out, and_708_out);
  or or_84 (or_84_out, and_709_out, and_710_out);
  or or_85 (or_85_out, and_711_out, and_712_out);
  or or_86 (or_86_out, and_713_out, and_714_out);
  or or_87 (or_87_out, and_715_out, and_716_out);
  or or_88 (or_88_out, and_717_out, and_718_out);
  or or_89 (or_89_out, and_719_out, and_720_out);
  or or_90 (or_90_out, and_721_out, and_722_out);
  or or_91 (or_91_out, or_41_out, and_723_out);
  or or_92 (or_92_out, and_724_out, and_725_out);
  or or_93 (or_93_out, and_726_out, and_727_out);
  or or_94 (or_94_out, and_728_out, and_729_out);
  or or_95 (or_95_out, and_730_out, and_731_out);
  or or_96 (or_96_out, and_732_out, and_733_out);
  or or_97 (or_97_out, and_734_out, and_735_out);
  or or_98 (or_98_out, and_736_out, and_737_out);
  or or_99 (T3, or_43_out, or_44_out);
  or or_100 (T2, or_45_out, or_46_out);
  or or_101 (or_101_out, or_47_out, or_48_out);
  or or_102 (or_102_out, or_49_out, or_50_out);
  or or_103 (or_103_out, or_51_out, or_52_out);
  or or_104 (or_104_out, or_53_out, or_54_out);
  or or_105 (or_105_out, or_55_out, or_56_out);
  or or_106 (or_106_out, or_57_out, or_58_out);
  or or_107 (or_107_out, or_59_out, or_60_out);
  or or_108 (or_108_out, or_61_out, or_62_out);
  or or_109 (or_109_out, or_63_out, or_64_out);
  or or_110 (or_110_out, or_65_out, or_66_out);
  or or_111 (or_111_out, or_67_out, or_68_out);
  or or_112 (or_112_out, or_69_out, or_70_out);
  or or_113 (or_113_out, or_71_out, or_72_out);
  or or_114 (or_114_out, or_73_out, or_74_out);
  or or_115 (or_115_out, or_75_out, or_76_out);
  or or_116 (or_116_out, or_77_out, or_78_out);
  or or_117 (or_117_out, or_79_out, or_80_out);
  or or_118 (or_118_out, or_81_out, or_82_out);
  or or_119 (or_119_out, or_83_out, or_84_out);
  or or_120 (or_120_out, or_85_out, or_86_out);
  or or_121 (or_121_out, or_87_out, or_88_out);
  or or_122 (or_122_out, or_89_out, or_90_out);
  or or_123 (or_123_out, or_91_out, or_92_out);
  or or_124 (or_124_out, or_93_out, or_94_out);
  or or_125 (or_125_out, or_95_out, or_96_out);
  or or_126 (or_126_out, or_97_out, or_98_out);
  or or_127 (T1, or_101_out, or_102_out);
  or or_128 (or_128_out, or_103_out, or_104_out);
  or or_129 (or_129_out, or_105_out, or_106_out);
  or or_130 (or_130_out, or_107_out, or_108_out);
  or or_131 (or_131_out, or_109_out, or_110_out);
  or or_132 (or_132_out, or_111_out, or_112_out);
  or or_133 (or_133_out, or_113_out, or_114_out);
  or or_134 (or_134_out, or_115_out, or_116_out);
  or or_135 (or_135_out, or_117_out, or_118_out);
  or or_136 (or_136_out, or_119_out, or_120_out);
  or or_137 (or_137_out, or_121_out, or_122_out);
  or or_138 (or_138_out, or_123_out, or_124_out);
  or or_139 (or_139_out, or_125_out, or_126_out);
  or or_140 (T0, or_128_out, or_129_out);
  or or_141 (U3, or_130_out, or_131_out);
  or or_142 (or_142_out, or_132_out, or_133_out);
  or or_143 (U2, or_142_out, or_144_out);
  or or_144 (or_144_out, or_134_out, or_135_out);
  or or_145 (or_145_out, or_136_out, or_137_out);
  or or_146 (U1, or_145_out, or_147_out);
  or or_147 (or_147_out, or_138_out, or_139_out);

  assign H2 = 1'b0;
  assign H3 = 1'b0;
  assign U0 = H;
endmodule

module BCD_to_7_segment_display (
  input  MSB,
  input  in_2,
  input  in_3,
  input  LSB,
  output out_5,
  output out_6,
  output out_7,
  output out_8,
  output out_9,
  output out_10,
  output out_11
);

  wire and_1_out, and_2_out, and_3_out, and_4_out, and_5_out, and_6_out, and_7_out, and_8_out, and_9_out,
       and_10_out, and_11_out, and_12_out, and_13_out, and_14_out, and_15_out, and_16_out, not_1_out,
       not_2_out, not_3_out, not_4_out, not_5_out, not_6_out, not_7_out, not_8_out, not_9_out, not_10_out,
       not_11_out, not_12_out, not_13_out, not_14_out, not_15_out, not_16_out, not_17_out, not_18_out,
       not_19_out, not_20_out, not_21_out;

  not not_1 (not_1_out, in_2);
  and and_1 (and_1_out, not_1_out, not_2_out);
  not not_2 (not_2_out, LSB);
  and and_2 (and_2_out, in_2, LSB);
  not not_3 (not_3_out, in_2);
  not not_4 (not_4_out, in_3);
  and and_3 (and_3_out, not_4_out, not_5_out);
  not not_5 (not_5_out, LSB);
  and and_4 (and_4_out, in_3, LSB);
  not not_6 (not_6_out, in_3);
  or or_1 (out_7, not_6_out, LSB, in_2);
  not not_7 (not_7_out, in_2);
  and and_5 (and_5_out, not_7_out, not_8_out);
  not not_8 (not_8_out, LSB);
  not not_9 (not_9_out, in_2);
  and and_6 (and_6_out, not_9_out, in_3);
  and and_7 (and_7_out, in_3, not_10_out);
  not not_10 (not_10_out, LSB);
  not not_11 (not_11_out, in_3);
  and and_8 (and_8_out, in_2, not_11_out, LSB);
  not not_12 (not_12_out, in_2);
  and and_9 (and_9_out, not_12_out, not_13_out);
  not not_13 (not_13_out, LSB);
  and and_10 (and_10_out, in_3, not_14_out);
  not not_14 (not_14_out, LSB);
  not not_15 (not_15_out, in_3);
  and and_11 (and_11_out, not_15_out, not_16_out);
  not not_16 (not_16_out, LSB);
  and and_12 (and_12_out, in_2, not_17_out);
  not not_17 (not_17_out, in_3);
  and and_13 (and_13_out, in_2, not_18_out);
  not not_18 (not_18_out, LSB);
  not not_19 (not_19_out, in_2);
  and and_14 (and_14_out, not_19_out, in_3);
  and and_15 (and_15_out, in_2, not_20_out);
  not not_20 (not_20_out, in_3);
  and and_16 (and_16_out, in_2, not_21_out);
  not not_21 (not_21_out, LSB);
  or or_2 (out_5, and_1_out, in_3, and_2_out, MSB);
  or or_3 (out_6, not_3_out, and_3_out, and_4_out);
  or or_4 (out_8, and_5_out, and_6_out, and_7_out, and_8_out, MSB);
  or or_5 (out_9, and_9_out, and_10_out);
  or or_6 (out_10, and_11_out, and_12_out, and_13_out, MSB);
  or or_7 (out_11, and_14_out, and_15_out, and_16_out, MSB);
endmodule

module _4_bit_D_flip_flop (
  input  CLK,
  input  LSB,
  input  in_3,
  input  in_4,
  input  MSB,
  output LSB_2,
  output out_7,
  output out_8,
  output MSB_2
);

  D_Flip_Flop d_ff_1 (.clk(CLK), .D(LSB), .Q(LSB_2));  // open: Qn, preset, en, reset
  D_Flip_Flop d_ff_2 (.clk(CLK), .D(in_3), .Q(out_7));  // open: Qn, preset, en, reset
  D_Flip_Flop d_ff_3 (.clk(CLK), .D(in_4), .Q(out_8));  // open: Qn, preset, en, reset
  D_Flip_Flop d_ff_4 (.clk(CLK), .D(MSB), .Q(MSB_2));  // open: Qn, preset, en, reset
endmodule

module initial_calc (
  input  [1:0] ROAD_QUALITY,
  input  DRIVER_S_QUALITY,
  input  [1:0] TYPE_OF_VEHICLE,
  output [3:0] out_4,
  output [3:0] out_5,
  output [3:0] out_6
);

  wire not_1_out, not_2_out, not_3_out, not_4_out;
  wire [1:1] not_12_out;
  wire [3:0] divider_1_out, divider_2_out, divider_3_out, divider_4_out, divider_5_out, divider_6_out,
       divider_7_out, n4_bit_multiplier_1_out_9;
  wire [3:1] not_6_out, not_7_out, not_8_out, not_9_out, not_10_out, not_11_out, not_13_out, not_14_out,
       not_15_out;
  wire [7:0] n4_bit_multiplier_2_out_9;
  wire [7:4] n4_bit_multiplier_1_out_9_2;

  not not_1 (not_1_out, TYPE_OF_VEHICLE[1]);
  not not_2 (not_2_out, TYPE_OF_VEHICLE[0]);
  not not_3 (not_3_out, ROAD_QUALITY[1]);
  not not_4 (not_4_out, ROAD_QUALITY[0]);
  and and_1 (not_13_out[3], not_1_out, not_2_out);
  and and_2 (not_6_out[3], not_1_out, TYPE_OF_VEHICLE[0]);
  and and_3 (not_7_out[3], not_2_out, TYPE_OF_VEHICLE[1]);
  and and_4 (not_8_out[3], TYPE_OF_VEHICLE[0], TYPE_OF_VEHICLE[1]);
  and and_5 (not_14_out[3], not_3_out, not_4_out);
  and and_6 (not_9_out[3], not_3_out, ROAD_QUALITY[0]);
  and and_7 (not_10_out[3], not_4_out, ROAD_QUALITY[1]);
  and and_8 (not_11_out[3], ROAD_QUALITY[0], ROAD_QUALITY[1]);
  not not_5 (not_15_out[3], DRIVER_S_QUALITY);
  not not_6 (not_6_out[1], not_6_out[3]);
  not not_7 (not_7_out[1], not_7_out[3]);
  not not_8 (not_8_out[1], not_8_out[3]);
  not not_9 (not_9_out[1], not_9_out[3]);
  not not_10 (not_10_out[1], not_10_out[3]);
  not not_11 (not_11_out[1], not_11_out[3]);
  not not_12 (not_12_out[1], DRIVER_S_QUALITY);
  not not_13 (not_13_out[1], not_13_out[3]);
  not not_14 (not_14_out[1], not_14_out[3]);
  not not_15 (not_15_out[1], not_15_out[3]);
  _4_bit_multiplier u_4_bit_multiplier_1 (
    .in_1(divider_1_out[0]), .in_2(divider_1_out[1]), .in_3(divider_1_out[2]), .in_4(divider_1_out[3]),
    .in_5(1'b1), .in_6(1'b1), .in_7(1'b0), .in_8(1'b0),
    .out_9({n4_bit_multiplier_1_out_9_2, n4_bit_multiplier_1_out_9}));
  Divider #(.width(4)) divider_1 (
    .a({{2{not_6_out[3]}}, {2{not_6_out[1]}}}), .b(4'b0100), .out(divider_1_out));  // open: upper, rem
  Divider #(.width(4)) divider_2 (
    .a({{2{not_7_out[3]}}, {2{not_7_out[1]}}}), .b(4'b0010), .out(divider_2_out));  // open: upper, rem
  Divider #(.width(4)) divider_3 (
    .a({{2{not_8_out[3]}}, {2{not_8_out[1]}}}), .b(4'b0100), .out(divider_3_out));  // open: upper, rem
  _4_bit_multiplier u_4_bit_multiplier_2 (
    .in_1(divider_4_out[0]), .in_2(divider_4_out[1]), .in_3(divider_4_out[2]), .in_4(divider_4_out[3]),
    .in_5(1'b1), .in_6(1'b1), .in_7(1'b0), .in_8(1'b0), .out_9(n4_bit_multiplier_2_out_9));
  Divider #(.width(4)) divider_4 (
    .a({{2{not_9_out[3]}}, {2{not_9_out[1]}}}), .b(4'b0100), .out(divider_4_out));  // open: upper, rem
  Divider #(.width(4)) divider_5 (
    .a({{2{not_10_out[3]}}, {2{not_10_out[1]}}}), .b(4'b0010), .out(divider_5_out));  // open: upper, rem
  Divider #(.width(4)) divider_6 (
    .a({{2{not_11_out[3]}}, {2{not_11_out[1]}}}), .b(4'b0100), .out(divider_6_out));  // open: upper, rem
  Divider #(.width(4)) divider_7 (
    .a({{2{DRIVER_S_QUALITY}}, {2{not_12_out[1]}}}), .b(4'b0010), .out(divider_7_out));  // open: upper, rem
  Multiplexer #(.width(4)) multiplexer_1 (
    .in0({{2{not_15_out[3]}}, {2{not_15_out[1]}}}), .in1(divider_7_out), .out(out_5), .sel(DRIVER_S_QUALITY));  // open: en
  Multiplexer #(.select(2), .width(4)) multiplexer_2 (
    .in0({{2{not_13_out[3]}}, {2{not_13_out[1]}}}), .in1(n4_bit_multiplier_1_out_9), .in2(divider_2_out),
    .in3(divider_3_out), .out(out_6), .sel(TYPE_OF_VEHICLE));  // open: en
  Multiplexer #(.select(2), .width(4)) multiplexer_3 (
    .in0({{2{not_14_out[3]}}, {2{not_14_out[1]}}}), .in1(n4_bit_multiplier_2_out_9[3:0]),
    .in2(divider_5_out), .in3(divider_6_out), .out(out_4), .sel(ROAD_QUALITY));  // open: en
endmodule

module comparator (
  input  [3:0] in_1,
  input  [3:0] in_2,
  output less_than,
  output equal
);

  wire and_1_out, and_2_out, and_3_out, and_4_out, and_5_out, and_6_out, comparator_1_eq, comparator_1_gt,
       comparator_2_eq, comparator_2_gt, comparator_3_eq, comparator_3_gt, comparator_4_eq, comparator_4_gt,
       comparator_5_eq, comparator_5_gt, comparator_6_eq, comparator_6_gt, or_1_out;

  Comparator #(.width(1)) comparator_1 (.a(1'b0), .b(1'b0), .gt(comparator_1_gt), .eq(comparator_1_eq));  // open: lt
  Comparator #(.width(1)) comparator_2 (.a(1'b0), .b(1'b0), .gt(comparator_2_gt), .eq(comparator_2_eq));  // open: lt
  Comparator #(.width(1)) comparator_3 (
    .a(in_1[3]), .b(in_2[3]), .gt(comparator_3_gt), .eq(comparator_3_eq));  // open: lt
  Comparator #(.width(1)) comparator_4 (
    .a(in_1[2]), .b(in_2[2]), .gt(comparator_4_gt), .eq(comparator_4_eq));  // open: lt
  Comparator #(.width(1)) comparator_5 (
    .a(in_1[1]), .b(in_2[1]), .gt(comparator_5_gt), .eq(comparator_5_eq));  // open: lt
  Comparator #(.width(1)) comparator_6 (
    .a(in_1[0]), .b(in_2[0]), .gt(comparator_6_gt), .eq(comparator_6_eq));  // open: lt
  and and_1 (and_1_out, comparator_1_eq, comparator_2_gt);
  and and_2 (and_2_out, comparator_1_eq, comparator_2_eq, comparator_3_gt);
  and and_3 (and_3_out, comparator_1_eq, comparator_2_eq, comparator_3_eq, comparator_4_gt);
  and and_4 (and_4_out, comparator_1_eq, comparator_2_eq, comparator_3_eq, comparator_4_eq, comparator_5_gt);
  and and_5 (and_5_out, comparator_1_eq, comparator_2_eq, comparator_3_eq, comparator_4_eq, comparator_5_eq);
  or or_1 (or_1_out, and_1_out, and_2_out, and_3_out, and_4_out, and_6_out);
  and and_6 (and_6_out, comparator_6_gt, and_5_out);
  and and_7 (equal, and_5_out, comparator_6_eq);
  or or_2 (less_than, comparator_1_gt, or_1_out);
endmodule

module _4_bit_adder_cun_subtractor (
  input  B2,
  input  A2,
  input  B3,
  input  A3,
  input  B1,
  input  A1,
  input  B0,
  input  A0,
  input  in_9,
  output out_10,
  output out_11,
  output out_12,
  output out_13,
  output out_14
);

  wire full_adder_2_cout, full_adder_3_cout, full_adder_4_cout, xor_1_out, xor_2_out, xor_3_out, xor_4_out;

  xor xor_1 (xor_1_out, B3, in_9);
  full_adder full_adder_1 (.A(A3), .B(xor_1_out), .C(full_adder_2_cout), .SUM(out_11), .COUT(out_10));
  xor xor_2 (xor_2_out, B2, in_9);
  full_adder full_adder_2 (.A(A2), .B(xor_2_out), .C(full_adder_3_cout), .SUM(out_12), .COUT(full_adder_2_cout));
  xor xor_3 (xor_3_out, B1, in_9);
  full_adder full_adder_3 (.A(A1), .B(xor_3_out), .C(full_adder_4_cout), .SUM(out_13), .COUT(full_adder_3_cout));
  xor xor_4 (xor_4_out, B0, in_9);
  full_adder full_adder_4 (.A(A0), .B(xor_4_out), .C(in_9), .SUM(out_14), .COUT(full_adder_4_cout));
endmodule
module full_adder (
  input  A,
  input  B,
  input  C,
  output SUM,
  output COUT
);

  wire and_1_out, and_2_out, and_3_out, and_4_out, and_5_out, and_6_out, and_7_out, and_8_out, and_9_out,
       and_10_out, and_11_out, not_1_out, not_2_out, not_3_out, not_4_out, not_5_out, not_6_out, or_1_out,
       or_3_out, or_4_out;

  not not_1 (not_1_out, A);
  not not_2 (not_2_out, B);
  not not_3 (not_3_out, A);
  not not_4 (not_4_out, B);
  and and_1 (and_1_out, B, C);
  and and_2 (and_2_out, A, C);
  and and_3 (and_3_out, not_1_out, not_2_out);
  and and_4 (and_4_out, not_3_out, B);
  not not_5 (not_5_out, C);
  and and_5 (and_5_out, A, not_4_out);
  not not_6 (not_6_out, C);
  and and_6 (and_6_out, A, B);
  or or_1 (or_1_out, and_1_out, and_2_out);
  and and_7 (and_7_out, A, B);
  and and_8 (and_8_out, and_3_out, C);
  and and_9 (and_9_out, and_4_out, not_5_out);
  and and_10 (and_10_out, and_5_out, not_6_out);
  and and_11 (and_11_out, and_6_out, C);
  or or_2 (COUT, or_1_out, and_7_out);
  or or_3 (or_3_out, and_8_out, and_9_out);
  or or_4 (or_4_out, and_10_out, and_11_out);
  or or_5 (SUM, or_3_out, or_4_out);
endmodule
