// Logisim project SIMPLIFIED CIRCUIT LOGISIM (3).circ as structural Verilog: 7 circuits, main circuit main
module main (
  input  MILEAGE,
  input  in_2,
  input  FUEL,
  input  in_4,
  input  in_5,
  input  DISTANCE,
  input  [1:0] in_7,
  input  in_8,
  output [1:0] Fuel_Remaining
);

  wire BCD_to_7_seg_decoder_s, BCD_to_7_seg_decoder_u, BCD_to_7_seg_decoder_v, BCD_to_7_seg_decoder_w,
       BCD_to_7_seg_decoder_x, BCD_to_7_seg_decoder_y, BCD_to_7_seg_decoder_z, clock_1_out,
       d_flip_flop_1_lsb_2, d_flip_flop_1_out_7, divider_c0, divider_c1, multiplier_c0, multiplier_c1,
       multiplier_c2, multiplier_c3, n2_bit_comparator_1_aeb, n2_bit_comparator_1_alb, or_1_out;

  _2_BIT_DIVIDER divider (.A1(in_5), .A0(DISTANCE), .B1(MILEAGE), .B0(in_2), .C1(divider_c1), .C0(divider_c0));
  _2_BIT_MULTIPLER multiplier (
    .A1(MILEAGE), .A0(in_2), .B1(FUEL), .B0(in_4), .C3(multiplier_c3), .C2(multiplier_c2),
    .C1(multiplier_c1), .C0(multiplier_c0));
  _2_BIT_SUBTRACTOR subtractor (
    .A1(FUEL), .A0(in_4), .B1(divider_c1), .B0(divider_c0), .D1(Fuel_Remaining[1]), .D0(Fuel_Remaining[0]));  // open: B_OUT
  Clock clock_1 (.out(clock_1_out));
  BCD_to_7_segment_display BCD_to_7_seg_decoder (
    .MSB(multiplier_c3), .a(multiplier_c2), .b(multiplier_c1), .LSB(multiplier_c0),
    .x(BCD_to_7_seg_decoder_x), .y(BCD_to_7_seg_decoder_y), .z(BCD_to_7_seg_decoder_z),
    .u(BCD_to_7_seg_decoder_u), .v(BCD_to_7_seg_decoder_v), .w(BCD_to_7_seg_decoder_w),
    .s(BCD_to_7_seg_decoder_s));
  d_flip_flop d_flip_flop_1 (
    .CLK(clock_1_out), .LSB(in_7[0]), .in_3(in_7[1]), .in_4(in_8), .MSB(in_8), .LSB_2(d_flip_flop_1_lsb_2),
    .out_7(d_flip_flop_1_out_7));  // open: out_8, MSB_2
  _2_BIT_COMPARATOR u_2_bit_comparator_1 (
    .A1(d_flip_flop_1_out_7), .A0(d_flip_flop_1_lsb_2), .B1(Fuel_Remaining[1]), .B0(Fuel_Remaining[0]),
    .ALB(n2_bit_comparator_1_alb), .AEB(n2_bit_comparator_1_aeb));  // open: AGB
  _7_Segment_Display u_7_segment_display_1 (
    .g(BCD_to_7_seg_decoder_s), .f(BCD_to_7_seg_decoder_w), .a(BCD_to_7_seg_decoder_x),
    .b(BCD_to_7_seg_decoder_y), .e(BCD_to_7_seg_decoder_v), .d(BCD_to_7_seg_decoder_u),
    .c(BCD_to_7_seg_decoder_z));  // open: dp
  LED led_1 (.in(or_1_out));
  or or_1 (or_1_out, n2_bit_comparator_1_alb, n2_bit_comparator_1_aeb);

  // Notes on the sheet:
  //   DIGITAL FUEL GAUGE WITH ADVANCED MONITORING FEATURES
  //   SIMPLIFIED CIRCUIT
  //   TEAM ID: T22
  //   TEAM ID: T22
  //   TEAM ID: T22
  //   AADITYA YADAV 231CS102
  //   CHETAN KUMAR SAH 231CS102
  //   CHETAN KUMAR SAH 231CS102
  //   CHETAN KUMAR SAH 231CS102
  //   GIRISH SHARMA 231CS123
  //   GIRISH SHARMA 231CS123
  //   GIRISH SHARMA 231CS123
  //   2. ENTER DISTANCE. IT WILL CALCULATE THE FUEL CONSUMED BY THE VEHICLE
  //   3. NOW, IT WILL CALCULATE AND DISPLAY THE REMAINING FUEL IN THE VEHICLE.
  //   4. LED WILL GLOW IF REMAINING FUEL IS LESS THAN THE THRESHOLD FUEL VALUE
  //   Maximum Range
  //   INSTRUCTIONS
  //   1. ENTER MILEAGE AND FUEL. IT WILL CALCULATE AND SHOW THE MAXIMUM RANGE OF THE VEHIC;E.
endmodule

module _2_BIT_MULTIPLER (
  input  A1,
  input  A0,
  input  B1,
  input  B0,
  output C3,
  output C2,
  output C1,
  output C0
);

  wire and_2_out, and_3_out, and_4_out, and_5_out, and_6_out, not_1_out, not_2_out, not_3_out, not_4_out,
       not_5_out;

  and and_1 (C3, A1, A0, B1, B0);
  not not_1 (not_1_out, A0);
  and and_2 (and_2_out, A1, not_1_out, B1);
  and and_3 (and_3_out, A1, B1, not_2_out);
  not not_2 (not_2_out, B0);
  not not_3 (not_3_out, A1);
  and and_4 (and_4_out, not_3_out, A0, B1);
  and and_5 (and_5_out, A0, B1, not_4_out);
  not not_4 (not_4_out, B0);
  not not_5 (not_5_out, B1);
  and and_6 (and_6_out, A1, not_5_out, B0);
  and and_7 (C0, A0, B0);
  or or_1 (C2, and_2_out, and_3_out);
  or or_2 (C1, and_4_out, and_5_out, and_6_out);
endmodule

module _2_BIT_DIVIDER (
  input  A1,
  input  A0,
  input  B1,
  input  B0,
  output C1,
  output C0
);

  wire and_1_out, and_2_out, and_3_out, not_1_out, not_2_out, not_3_out;

  not not_1 (not_1_out, A1);
  and and_1 (and_1_out, not_1_out, A0, B1);
  and and_2 (and_2_out, A0, B1, not_2_out);
  not not_2 (not_2_out, B0);
  and and_3 (and_3_out, A1, not_3_out, B0);
  not not_3 (not_3_out, B1);
  and and_4 (C0, A0, B0);
  or or_1 (C1, and_1_out, and_2_out, and_3_out);
endmodule

module _2_BIT_SUBTRACTOR (
  input  A1,
  input  A0,
  input  B1,
  input  B0,
  output D1,
  output D0,
  output B_OUT
);

  wire and_1_out, and_2_out, and_3_out, and_4_out, and_5_out, and_6_out, and_7_out, and_8_out, and_9_out,
       and_10_out, not_1_out, not_2_out, not_3_out, not_4_out, not_5_out, not_6_out, not_7_out, not_8_out,
       not_9_out, not_10_out, not_11_out;

  not not_1 (not_1_out, A1);
  and and_1 (and_1_out, not_1_out, B0);
  not not_2 (not_2_out, A1);
  and and_2 (and_2_out, not_2_out, B1);
  not not_3 (not_3_out, A0);
  and and_3 (and_3_out, not_3_out, B1, B0);
  not not_4 (not_4_out, B1);
  and and_4 (and_4_out, A1, not_4_out, not_5_out);
  not not_5 (not_5_out, B0);
  and and_5 (and_5_out, A1, A0, not_6_out);
  not not_6 (not_6_out, B1);
  not not_7 (not_7_out, A0);
  and and_6 (and_6_out, not_7_out, B0);
  and and_7 (and_7_out, A0, not_8_out);
  not not_8 (not_8_out, B0);
  not not_9 (not_9_out, A1);
  and and_8 (and_8_out, not_9_out, B0);
  not not_10 (not_10_out, A1);
  and and_9 (and_9_out, not_10_out, B1);
  not not_11 (not_11_out, A0);
  and and_10 (and_10_out, not_11_out, B1, B0);
  or or_1 (D1, and_1_out, and_2_out, and_3_out, and_4_out, and_5_out);
  or or_2 (D0, and_6_out, and_7_out);
  or or_3 (B_OUT, and_8_out, and_9_out, and_10_out);
endmodule

module _2_BIT_COMPARATOR (
  input  A1,
  input  A0,
  input  B1,
  input  B0,
  output AGB,
  output ALB,
  output AEB
);

  wire and_1_out, and_2_out, and_3_out, and_4_out, and_5_out, and_6_out, and_7_out, and_8_out, and_9_out,
       and_10_out, not_1_out, not_2_out, not_3_out, not_4_out, not_5_out, not_6_out, not_7_out, not_8_out,
       not_9_out, not_10_out, not_11_out, not_12_out, not_13_out, not_14_out, not_15_out, not_16_out;

  and and_1 (and_1_out, A0, not_1_out, not_2_out);
  not not_1 (not_1_out, B1);
  not not_2 (not_2_out, B0);
  and and_2 (and_2_out, A1, not_3_out);
  not not_3 (not_3_out, B1);
  and and_3 (and_3_out, A1, A0, not_4_out);
  not not_4 (not_4_out, B0);
  not not_5 (not_5_out, A1);
  not not_6 (not_6_out, A0);
  and and_4 (and_4_out, not_5_out, not_6_out, B0);
  not not_7 (not_7_out, A1);
  and and_5 (and_5_out, not_7_out, B1);
  not not_8 (not_8_out, A0);
  and and_6 (and_6_out, not_8_out, B1, B0);
  not not_9 (not_9_out, A1);
  not not_10 (not_10_out, A0);
  not not_11 (not_11_out, B1);
  not not_12 (not_12_out, B0);
  not not_13 (not_13_out, A1);
  not not_14 (not_14_out, B1);
  not not_15 (not_15_out, A0);
  not not_16 (not_16_out, B0);
  or or_1 (AGB, and_1_out, and_2_out, and_3_out);
  or or_2 (ALB, and_4_out, and_5_out, and_6_out);
  and and_7 (and_7_out, not_9_out, not_10_out, not_11_out, not_12_out);
  and and_8 (and_8_out, not_13_out, A0, not_14_out, B0);
  and and_9 (and_9_out, A1, not_15_out, B1, not_16_out);
  and and_10 (and_10_out, A1, A0, B1, B0);
  or or_3 (AEB, and_7_out, and_8_out, and_9_out, and_10_out);
endmodule

module BCD_to_7_segment_display (
  input  MSB,
  input  a,
  input  b,
  input  LSB,
  output x,
  output y,
  output z,
  output u,
  output v,
  output w,
  output s
);

  wire and_1_out, and_2_out, and_3_out, and_4_out, and_5_out, and_6_out, and_7_out, and_8_out, and_9_out,
       and_10_out, and_11_out, and_12_out, and_13_out, and_14_out, and_15_out, and_16_out, not_1_out,
       not_2_out, not_3_out, not_4_out, not_5_out, not_6_out, not_7_out, not_8_out, not_9_out, not_10_out,
       not_11_out, not_12_out, not_13_out, not_14_out, not_15_out, not_16_out, not_17_out, not_18_out,
       not_19_out, not_20_out, not_21_out;

  not not_1 (not_1_out, a);
  and and_1 (and_1_out, not_1_out, not_2_out);
  not not_2 (not_2_out, LSB);
  and and_2 (and_2_out, a, LSB);
  not not_3 (not_3_out, a);
  not not_4 (not_4_out, b);
  and and_3 (and_3_out, not_4_out, not_5_out);
  not not_5 (not_5_out, LSB);
  and and_4 (and_4_out, b, LSB);
  not not_6 (not_6_out, b);
  or or_1 (z, not_6_out, LSB, a);
  not not_7 (not_7_out, a);
  and and_5 (and_5_out, not_7_out, not_8_out);
  not not_8 (not_8_out, LSB);
  not not_9 (not_9_out, a);
  and and_6 (and_6_out, not_9_out, b);
  and and_7 (and_7_out, b, not_10_out);
  not not_10 (not_10_out, LSB);
  and and_8 (and_8_out, a, not_11_out, LSB);
  not not_11 (not_11_out, b);
  not not_12 (not_12_out, a);
  and and_9 (and_9_out, not_12_out, not_13_out);
  not not_13 (not_13_out, LSB);
  and and_10 (and_10_out, b, not_14_out);
  not not_14 (not_14_out, LSB);
  not not_15 (not_15_out, b);
  and and_11 (and_11_out, not_15_out, not_16_out);
  not not_16 (not_16_out, LSB);
  and and_12 (and_12_out, a, not_17_out);
  not not_17 (not_17_out, b);
  and and_13 (and_13_out, a, not_18_out);
  not not_18 (not_18_out, LSB);
  not not_19 (not_19_out, a);
  and and_14 (and_14_out, not_19_out, b);
  and and_15 (and_15_out, a, not_20_out);
  not not_20 (not_20_out, b);
  and and_16 (and_16_out, a, not_21_out);
  not not_21 (not_21_out, LSB);
  or or_2 (x, and_1_out, b, and_2_out, MSB);
  or or_3 (y, not_3_out, and_3_out, and_4_out);
  or or_4 (u, and_5_out, and_6_out, and_7_out, and_8_out, MSB);
  or or_5 (v, and_9_out, and_10_out);
  or or_6 (w, and_11_out, and_12_out, and_13_out, MSB);
  or or_7 (s, and_14_out, and_15_out, and_16_out, MSB);
endmodule

module d_flip_flop (
  input  CLK,
  input  LSB,
  input  in_3,
  input  in_4,
  input  MSB,
  output LSB_2,
  output out_7,
  output out_8,
  output MSB_2
);

  D_Flip_Flop d_ff_1 (.clk(CLK), .D(LSB), .Q(LSB_2));  // open: Qn, preset, en, reset
  D_Flip_Flop d_ff_2 (.clk(CLK), .D(in_3), .Q(out_7));  // open: Qn, preset, en, reset
  D_Flip_Flop d_ff_3 (.clk(CLK), .D(in_4), .Q(out_8));  // open: Qn, preset, en, reset
  D_Flip_Flop d_ff_4 (.clk(CLK), .D(MSB), .Q(MSB_2));  // open: Qn, preset, en, reset
endmodule
